// Logisim project 8位偶校验传输测试实验.circ as structural Verilog: 4 circuits, main circuit 偶校验传输测试实验
module \偶校验传输测试实验  (
);

  wire and_1_out, and_2_out, C, CLK, CLR_out, OK;
  wire [7:0] counter_1_q, rom_1_data, \偶校验检错电路_1_数据位 ;
  wire [8:0] \偶校验编码电路_1_偶校验编码 , \随机加扰电路_1_加扰后数据 , \随机加扰电路_1_随机加扰屏蔽字 ;

  Counter #(.behavior("old")) counter_1 (
    .Q(counter_1_q), .clk(CLK), .clr(CLR_out));  // open: load, D, count, carry, preset
  Button CLR (.out(CLR_out));
  Clock \u_时钟  (.out(CLK));
  ROM #(.Select("high")) rom_1 (.addr(counter_1_q), .data(rom_1_data));
  // Probe on rom_1_data
  \偶校验编码电路  \u_偶校验编码电路_1  (.\原始数据 (rom_1_data), .\偶校验编码 (\偶校验编码电路_1_偶校验编码 ));
  // Probe on \偶校验编码电路_1_偶校验编码 
  // Probe on \随机加扰电路_1_随机加扰屏蔽字 
  \随机加扰电路  \u_随机加扰电路_1  (
    .\_9位输入 (\偶校验编码电路_1_偶校验编码 ), .\随机加扰屏蔽字 (\随机加扰电路_1_随机加扰屏蔽字 ), .\加扰后数据 (\随机加扰电路_1_加扰后数据 ), .CLK(CLK));
  // Probe on \随机加扰电路_1_加扰后数据 
  \偶校验检错电路  \u_偶校验检错电路_1  (.\检错位 (C), .\偶校验编码 (\随机加扰电路_1_加扰后数据 ), .\数据位 (\偶校验检错电路_1_数据位 ));
  // Probe on \偶校验检错电路_1_数据位 
  Comparator comparator_1 (.a(rom_1_data), .b(\偶校验检错电路_1_数据位 ), .eq(OK));  // open: gt, lt
  and and_1 (and_1_out, ~OK, ~C);  // AND_Gate
  and and_2 (and_2_out, C, OK);
  LED \u_数据正确  (.in(OK));
  LED \u_漏报  (.in(and_1_out));
  LED \u_校验位出错  (.in(and_2_out));
  LED \u_检错位  (.in(C));

  // Notes on the sheet:
  //   发送方
  //   计数器
  //   ROM存储器
  //   contents of rom_1 (hex, n*v repeats v):
  //   80*f3
  //   电路功能：按“CLR”将计数器清零；按“时钟”2次，计数器加1，ROM存储器送出1个汉字的国标码。会有4种情况出现：
  //   1、数据正确=1（红灯）、检错位=0（白灯），表示没有错误（干扰屏蔽字=0），接收方与发送方显示的汉字相同
  //   3、数据正确=0（白灯）、检错位=1（红灯），表示检出错误，接收方与发送方显示的汉字不同
  //   4、数据正确=1（红灯）、检错位=1（红灯），表示校验位出错、数据位没有出错，接收方与发送方显示的汉字相同
  //   8位偶校验传输测试实验
  //   2、数据正确=0（白灯）、检错位=0（白灯），误报=1（红灯），表示误报（没有检出错，但是接收到的数据却出错了），接收方与发送方显示的汉字不同
  //   比较器
  //   接收方
endmodule

// 偶校验编码
module \偶校验编码电路  (
  input  [7:0] \原始数据 ,
  output [8:0] \偶校验编码 
);

  wire xor_1_out, xor_2_out, xor_3_out, xor_4_out, xor_5_out, xor_6_out;

  xor xor_1 (xor_1_out, \原始数据 [0], \原始数据 [1]);
  xor xor_2 (xor_2_out, \原始数据 [2], \原始数据 [3]);
  xor xor_3 (xor_3_out, \原始数据 [4], \原始数据 [5]);
  xor xor_4 (xor_4_out, \原始数据 [6], \原始数据 [7]);
  xor xor_5 (xor_5_out, xor_1_out, xor_2_out);
  xor xor_6 (xor_6_out, xor_3_out, xor_4_out);
  xor xor_7 (\偶校验编码 [8], xor_5_out, xor_6_out);

  assign \偶校验编码 [7:0] = \原始数据 ;

  // Other names for the same wires on the sheet: D1 = \原始数据 [0]; Data[7:0] = \原始数据 ; 校验码[8:0] = {\偶校验编码 [8], \原始数据 };
  //   D2 = \原始数据 [1]; D3 = \原始数据 [2]; D4 = \原始数据 [3]; D5 = \原始数据 [4]; D6 = \原始数据 [5]; D7 = \原始数据 [6]; D8 = \原始数据 [7]

  // Notes on the sheet:
  //   输入引脚区
  //   电路功能：实现8位数据位的偶校验编码
  //   输入：8位数据；输出：9位校验码（数据位+校验位）
  //   校验位
  //   偶校验编码电路
  //   输出引脚区
endmodule

// 偶校验检错
module \偶校验检错电路  (
  input  [8:0] \偶校验编码 ,
  output \检错位 ,
  output [7:0] \数据位 
);

  wire xor_1_out, xor_2_out, xor_3_out, xor_4_out, xor_5_out, xor_6_out;

  xor xor_1 (xor_1_out, \偶校验编码 [0], \偶校验编码 [1]);
  xor xor_2 (xor_2_out, \偶校验编码 [2], \偶校验编码 [3]);
  xor xor_3 (xor_3_out, \偶校验编码 [4], \偶校验编码 [5]);
  xor xor_4 (xor_4_out, \偶校验编码 [6], \偶校验编码 [7]);
  xor xor_5 (xor_5_out, xor_1_out, xor_2_out);
  xor xor_6 (xor_6_out, xor_3_out, xor_4_out);
  xor xor_7 (\检错位 , xor_5_out, xor_6_out);

  assign \数据位  = \偶校验编码 [7:0];

  // Other names for the same wires on the sheet: D1 = \偶校验编码 [0]; D2 = \偶校验编码 [1]; D3 = \偶校验编码 [2]; D4 = \偶校验编码 [3];
  //   D5 = \偶校验编码 [4]; D6 = \偶校验编码 [5]; D7 = \偶校验编码 [6]; D8 = \偶校验编码 [7]; P1 = \偶校验编码 [8]

  // Notes on the sheet:
  //   输入引脚区
  //   电路功能：实现17位偶校验编码的检错以及数据提取
  //   输入：偶校验编码；输出：检错位、数据位
  //   偶校验检错电路
  //   输出引脚区
endmodule

// 随机加扰
module \随机加扰电路  (
  input  CLK,
  input  [8:0] \_9位输入 ,
  output [8:0] \随机加扰屏蔽字 ,
  output [8:0] \加扰后数据 
);

  wire [4:0] \随机数_2_out , \随机数_3_out , \随机数_out ;
  wire [8:0] or_1_out;
  wire [31:0] decoder_1_out31, decoder_2_out31, decoder_3_out31;

  Decoder #(.select(5), .enable("false")) decoder_1 (
    .out0(decoder_1_out31[31]), .out1(decoder_1_out31[30]), .out2(decoder_1_out31[29]),
    .out3(decoder_1_out31[28]), .out4(decoder_1_out31[27]), .out5(decoder_1_out31[26]),
    .out6(decoder_1_out31[25]), .out7(decoder_1_out31[24]), .out8(decoder_1_out31[23]),
    .out9(decoder_1_out31[22]), .out10(decoder_1_out31[21]), .out11(decoder_1_out31[20]),
    .out12(decoder_1_out31[19]), .out13(decoder_1_out31[18]), .out14(decoder_1_out31[17]),
    .out15(decoder_1_out31[16]), .out16(decoder_1_out31[15]), .out17(decoder_1_out31[14]),
    .out18(decoder_1_out31[13]), .out19(decoder_1_out31[12]), .out20(decoder_1_out31[11]),
    .out21(decoder_1_out31[10]), .out22(decoder_1_out31[9]), .out23(decoder_1_out31[8]),
    .out24(decoder_1_out31[7]), .out25(decoder_1_out31[6]), .out26(decoder_1_out31[5]),
    .out27(decoder_1_out31[4]), .out28(decoder_1_out31[3]), .out29(decoder_1_out31[2]),
    .out30(decoder_1_out31[1]), .out31(decoder_1_out31[0]), .sel(\随机数_out ));
  Random #(.width(5)) \u_随机数  (.clk(CLK), .out(\随机数_out ));  // open: next, clr
  Decoder #(.select(5), .enable("false")) decoder_2 (
    .out0(decoder_2_out31[31]), .out1(decoder_2_out31[30]), .out2(decoder_2_out31[29]),
    .out3(decoder_2_out31[28]), .out4(decoder_2_out31[27]), .out5(decoder_2_out31[26]),
    .out6(decoder_2_out31[25]), .out7(decoder_2_out31[24]), .out8(decoder_2_out31[23]),
    .out9(decoder_2_out31[22]), .out10(decoder_2_out31[21]), .out11(decoder_2_out31[20]),
    .out12(decoder_2_out31[19]), .out13(decoder_2_out31[18]), .out14(decoder_2_out31[17]),
    .out15(decoder_2_out31[16]), .out16(decoder_2_out31[15]), .out17(decoder_2_out31[14]),
    .out18(decoder_2_out31[13]), .out19(decoder_2_out31[12]), .out20(decoder_2_out31[11]),
    .out21(decoder_2_out31[10]), .out22(decoder_2_out31[9]), .out23(decoder_2_out31[8]),
    .out24(decoder_2_out31[7]), .out25(decoder_2_out31[6]), .out26(decoder_2_out31[5]),
    .out27(decoder_2_out31[4]), .out28(decoder_2_out31[3]), .out29(decoder_2_out31[2]),
    .out30(decoder_2_out31[1]), .out31(decoder_2_out31[0]), .sel(\随机数_2_out ));
  Random #(.width(5), .seed(18)) \u_随机数_2  (.clk(CLK), .out(\随机数_2_out ));  // open: next, clr
  Random #(.width(5), .seed(3)) \u_随机数_3  (.clk(CLK), .out(\随机数_3_out ));  // open: next, clr
  Decoder #(.select(5), .enable("false")) decoder_3 (
    .out0(decoder_3_out31[31]), .out1(decoder_3_out31[30]), .out2(decoder_3_out31[29]),
    .out3(decoder_3_out31[28]), .out4(decoder_3_out31[27]), .out5(decoder_3_out31[26]),
    .out6(decoder_3_out31[25]), .out7(decoder_3_out31[24]), .out8(decoder_3_out31[23]),
    .out9(decoder_3_out31[22]), .out10(decoder_3_out31[21]), .out11(decoder_3_out31[20]),
    .out12(decoder_3_out31[19]), .out13(decoder_3_out31[18]), .out14(decoder_3_out31[17]),
    .out15(decoder_3_out31[16]), .out16(decoder_3_out31[15]), .out17(decoder_3_out31[14]),
    .out18(decoder_3_out31[13]), .out19(decoder_3_out31[12]), .out20(decoder_3_out31[11]),
    .out21(decoder_3_out31[10]), .out22(decoder_3_out31[9]), .out23(decoder_3_out31[8]),
    .out24(decoder_3_out31[7]), .out25(decoder_3_out31[6]), .out26(decoder_3_out31[5]),
    .out27(decoder_3_out31[4]), .out28(decoder_3_out31[3]), .out29(decoder_3_out31[2]),
    .out30(decoder_3_out31[1]), .out31(decoder_3_out31[0]), .sel(\随机数_3_out ));
  assign or_1_out = decoder_1_out31[8:0] | decoder_2_out31[8:0];  // OR_Gate or_1, 9 bits wide
  assign \随机加扰屏蔽字  = or_1_out | decoder_3_out31[8:0];  // OR_Gate or_2, 9 bits wide
  assign \加扰后数据  = \随机加扰屏蔽字  ^ \_9位输入 ;  // XOR_Gate xor_1, 9 bits wide

  // Notes on the sheet:
  //   5-32译码器
  //   5-32译码器
  //   5-32译码器
  //   随机加扰电路
endmodule
