// Logisim project 8位循环冗余校验码（并行）实验.circ as structural Verilog: 4 circuits, main circuit CRC码传输测试实验1
module \CRC码传输测试实验1  (
  input  [7:0] \原始数据 
);

  wire CLK_out, comparator_1_eq, \crc并行解码电路_1__1位错 , \crc并行解码电路_1__2位错 , \crc并行解码电路_1_无错误 ;
  wire [7:0] \crc并行解码电路_1_纠错后数据 ;
  wire [13:0] \crc并行编码电路_1_crc校验码 , \随机干扰电路_1_加扰后数据 , \随机干扰电路_1_随机加扰屏蔽字 ;

  // Probe on \原始数据 
  // Probe on \crc并行编码电路_1_crc校验码 
  \CRC并行编码电路  \crc并行编码电路_1  (.\原始数据 (\原始数据 ), .\CRC校验码 (\crc并行编码电路_1_crc校验码 ));
  // Probe on \随机干扰电路_1_随机加扰屏蔽字 
  Clock CLK (.out(CLK_out));
  \随机干扰电路  \u_随机干扰电路_1  (
    .\随机加扰屏蔽字 (\随机干扰电路_1_随机加扰屏蔽字 ), .\_14位输入 (\crc并行编码电路_1_crc校验码 ), .\加扰后数据 (\随机干扰电路_1_加扰后数据 ), .CLK(CLK_out));
  LED \u_无错  (.in(\crc并行解码电路_1_无错误 ));
  // Probe on \随机干扰电路_1_加扰后数据 
  LED \_1位错  (.in(\crc并行解码电路_1__1位错 ));
  LED \_2位错  (.in(\crc并行解码电路_1__2位错 ));
  \CRC并行解码电路  \crc并行解码电路_1  (
    .\CRC编码 (\随机干扰电路_1_加扰后数据 ), .\无错误 (\crc并行解码电路_1_无错误 ), .\_1位错 (\crc并行解码电路_1__1位错 ),
    .\_2位错 (\crc并行解码电路_1__2位错 ), .\纠错后数据 (\crc并行解码电路_1_纠错后数据 ));
  // Probe on \crc并行解码电路_1_纠错后数据 
  Comparator comparator_1 (.a(\原始数据 ), .b(\crc并行解码电路_1_纠错后数据 ), .eq(comparator_1_eq));  // open: gt, lt
  LED \u_数据正确  (.in(comparator_1_eq));

  // Notes on the sheet:
  //   发送方
  //   电路功能：测试CRC编解码电路正确性
  //   1、无错：无错灯红色，数据正确灯红色，接收数据等于发送数据
  //   先设置原始数据，然后每按“CLK”按钮2次，产生1个随机干扰，观看4个指示灯，有4种情况：
  //   2、1位错：1位错灯红色，数据正确灯红色，接收数据等于发送数据（可以纠正1位错）
  //   3、2位错：2位错灯红色，数据正确灯白色，接收数据不等于发送数据（不能纠正1位错）
  //   4、2位错：2位错灯红色，数据正确灯红色，接收数据等于发送数据（可以纠正某些情况的2位错误）
  //   输入：16位原始数据             输出：16位解码后的数据，4个指示灯（无错、1位错、2位错、数据正确）
  //   CRC码传输测试实验1
  //   接收方
endmodule

// CRC编码
module \CRC并行编码电路  (
  input  [7:0] \原始数据 ,
  output [13:0] \CRC校验码 
);

  wire [4:0] multiplexer_1_out, multiplexer_2_out, multiplexer_3_out, multiplexer_4_out, multiplexer_5_out,
       multiplexer_6_out, multiplexer_7_out, multiplexer_8_out;

  Multiplexer #(.width(5)) multiplexer_1 (
    .in0({5{1'b0}}), .in1(5'b01110), .out(multiplexer_1_out), .sel(\原始数据 [7]));  // open: en
  Multiplexer #(.width(5)) multiplexer_2 (
    .in0({5{1'b0}}), .in1(5'b10001), .out(multiplexer_2_out), .sel(\原始数据 [5]));  // open: en
  Multiplexer #(.width(5)) multiplexer_3 (
    .in0({5{1'b0}}), .in1(5'b00111), .out(multiplexer_3_out), .sel(\原始数据 [6]));  // open: en
  assign \CRC校验码 [4:0] = multiplexer_1_out ^ multiplexer_3_out ^ multiplexer_2_out ^ multiplexer_4_out ^ multiplexer_5_out ^ multiplexer_6_out ^ multiplexer_7_out ^ multiplexer_8_out;  // XOR_Gate xor_1, 5 bits wide
  Multiplexer #(.width(5)) multiplexer_4 (
    .in0({5{1'b0}}), .in1(5'b11010), .out(multiplexer_4_out), .sel(\原始数据 [4]));  // open: en
  Multiplexer #(.width(5)) multiplexer_5 (
    .in0({5{1'b0}}), .in1(5'b01101), .out(multiplexer_5_out), .sel(\原始数据 [3]));  // open: en
  Multiplexer #(.width(5)) multiplexer_6 (
    .in0({5{1'b0}}), .in1(5'b10100), .out(multiplexer_6_out), .sel(\原始数据 [2]));  // open: en
  Multiplexer #(.width(5)) multiplexer_7 (
    .in0({5{1'b0}}), .in1(5'b01010), .out(multiplexer_7_out), .sel(\原始数据 [1]));  // open: en
  Multiplexer #(.width(5)) multiplexer_8 (
    .in0({5{1'b0}}), .in1(5'b00101), .out(multiplexer_8_out), .sel(\原始数据 [0]));  // open: en
  xor xor_2 (\CRC校验码 [13], \CRC校验码 [0], \CRC校验码 [1], \原始数据 [0], \原始数据 [1], \原始数据 [2], \原始数据 [3], \原始数据 [4], \原始数据 [5], \原始数据 [6], \原始数据 [7], \CRC校验码 [2], \CRC校验码 [3], \CRC校验码 [4]);

  assign \CRC校验码 [12:5] = \原始数据 ;

  // Other names for the same wires on the sheet: CRC编码[13:0] = {\CRC校验码 [13], \原始数据 , \CRC校验码 [4:0]};
  //   P1 = \CRC校验码 [0]; P2 = \CRC校验码 [1]; P3 = \CRC校验码 [2]; P4 = \CRC校验码 [3]; P5 = \CRC校验码 [4]; D1 = \原始数据 [0];
  //   D2 = \原始数据 [1]; D3 = \原始数据 [2]; D4 = \原始数据 [3]; D5 = \原始数据 [4]; D6 = \原始数据 [5]; D7 = \原始数据 [6]; D8 = \原始数据 [7];
  //   P6 = \CRC校验码 [13]

  // Notes on the sheet:
  //   电路功能：循环冗余校验编码电路                生成多项式=100101
  //   输入引脚区
  //   CRC并行编码电路
  //   输出引脚区
  //   输入：8位原始数据                             输出：14位循环冗余校验码（8位数据位+6位校验位）
endmodule

// CRC解码
module \CRC并行解码电路  (
  input  [13:0] \CRC编码 ,
  output \无错误 ,
  output \_1位错 ,
  output \_2位错 ,
  output [7:0] \纠错后数据 
);

  wire and_2_out, nor_1_out, xor_1_out, xor_2_out;
  wire [4:0] multiplexer_2_out, multiplexer_3_out, multiplexer_4_out, multiplexer_5_out, multiplexer_7_out,
       multiplexer_8_out, multiplexer_9_out, multiplexer_10_out, xor_3_out;
  wire [7:0] and_4_out, multiplexer_1_out, multiplexer_6_out;

  and and_1 (\_2位错 , ~xor_2_out, ~nor_1_out);  // AND_Gate
  xor xor_1 (xor_1_out, \CRC编码 [0], \CRC编码 [1], \CRC编码 [5], \CRC编码 [6], \CRC编码 [7], \CRC编码 [8], \CRC编码 [9], \CRC编码 [10], \CRC编码 [11], \CRC编码 [12], \CRC编码 [2], \CRC编码 [3], \CRC编码 [4]);
  xor xor_2 (xor_2_out, xor_1_out, \CRC编码 [13]);
  or or_1 (\_1位错 , xor_2_out, and_2_out);
  and and_2 (and_2_out, xor_2_out, ~nor_1_out);  // AND_Gate
  and and_3 (\无错误 , ~xor_2_out, nor_1_out);  // AND_Gate
  nor nor_1 (nor_1_out, xor_3_out[4], xor_3_out[3], xor_3_out[2], xor_3_out[1], xor_3_out[0]);
  Multiplexer #(.select(5), .width(8)) multiplexer_1 (
    .in0({8{1'b0}}), .in1({8{1'b0}}), .in2({8{1'b0}}), .in3({8{1'b0}}), .in4({8{1'b0}}), .in5(8'h1),
    .in6({8{1'b0}}), .in7(8'h40), .in8({8{1'b0}}), .in9({8{1'b0}}), .in10(8'h2), .in11({8{1'b0}}),
    .in12({8{1'b0}}), .in13(8'h8), .in14(8'h80), .in15({8{1'b0}}), .in16({8{1'b0}}), .in17(8'h20),
    .in18({8{1'b0}}), .in19({8{1'b0}}), .in20(8'h4), .in21({8{1'b0}}), .in22({8{1'b0}}), .in23({8{1'b0}}),
    .in24({8{1'b0}}), .in25({8{1'b0}}), .in26(8'h10), .in27({8{1'b0}}), .in28({8{1'b0}}), .in29({8{1'b0}}),
    .in30({8{1'b0}}), .in31({8{1'b0}}), .out(multiplexer_1_out), .sel(xor_3_out), .en(1'b1));
  assign xor_3_out = multiplexer_2_out ^ multiplexer_4_out ^ multiplexer_3_out ^ multiplexer_5_out ^ multiplexer_8_out ^ multiplexer_7_out ^ multiplexer_9_out ^ multiplexer_10_out ^ \CRC编码 [4:0];  // XOR_Gate xor_3, 5 bits wide
  Multiplexer #(.width(5)) multiplexer_2 (
    .in0({5{1'b0}}), .in1(5'b01110), .out(multiplexer_2_out), .sel(\CRC编码 [12]));  // open: en
  Multiplexer #(.width(5)) multiplexer_3 (
    .in0({5{1'b0}}), .in1(5'b10001), .out(multiplexer_3_out), .sel(\CRC编码 [10]));  // open: en
  Multiplexer #(.width(5)) multiplexer_4 (
    .in0({5{1'b0}}), .in1(5'b00111), .out(multiplexer_4_out), .sel(\CRC编码 [11]));  // open: en
  Multiplexer #(.width(5)) multiplexer_5 (
    .in0({5{1'b0}}), .in1(5'b11010), .out(multiplexer_5_out), .sel(\CRC编码 [9]));  // open: en
  Multiplexer #(.width(8)) multiplexer_6 (
    .in0({8{1'b0}}), .in1({8{1'b1}}), .out(multiplexer_6_out), .sel(\_1位错 ));  // open: en
  Multiplexer #(.width(5)) multiplexer_7 (
    .in0({5{1'b0}}), .in1(5'b10100), .out(multiplexer_7_out), .sel(\CRC编码 [7]));  // open: en
  Multiplexer #(.width(5)) multiplexer_8 (
    .in0({5{1'b0}}), .in1(5'b01101), .out(multiplexer_8_out), .sel(\CRC编码 [8]));  // open: en
  assign and_4_out = multiplexer_6_out & multiplexer_1_out;  // AND_Gate and_4, 8 bits wide
  Multiplexer #(.width(5)) multiplexer_9 (
    .in0({5{1'b0}}), .in1(5'b01010), .out(multiplexer_9_out), .sel(\CRC编码 [6]));  // open: en
  Multiplexer #(.width(5)) multiplexer_10 (
    .in0({5{1'b0}}), .in1(5'b00101), .out(multiplexer_10_out), .sel(\CRC编码 [5]));  // open: en
  assign \纠错后数据  = \CRC编码 [12:5] ^ and_4_out;  // XOR_Gate xor_4, 8 bits wide

  // Other names for the same wires on the sheet: CRC[13:0] = \CRC编码 ; P1 = \CRC编码 [0]; P2 = \CRC编码 [1];
  //   P3 = \CRC编码 [2]; P4 = \CRC编码 [3]; P5 = \CRC编码 [4]; D1 = \CRC编码 [5]; D2 = \CRC编码 [6]; D3 = \CRC编码 [7];
  //   D4 = \CRC编码 [8]; D5 = \CRC编码 [9]; D6 = \CRC编码 [10]; D7 = \CRC编码 [11]; D8 = \CRC编码 [12]; P6 = \CRC编码 [13]

  // Notes on the sheet:
  //   电路功能：实现22位CRC编码的数据解码，能判断无错误、1位错、2位错，1位错具有自动纠错功能        生成多项式=100101
  //   输入引脚区
  //   CRC并行解码电路
  //   输出引脚区
  //   输入：22位CRC编码    输出：16位纠错后的数据，错误标志（无错误、1位错、2位错）
endmodule

// 随机干扰
module \随机干扰电路  (
  input  CLK,
  input  [13:0] \_14位输入 ,
  output [13:0] \随机加扰屏蔽字 ,
  output [13:0] \加扰后数据 
);

  wire comparator_1_eq, not_1_out, pull_resistor_1_node, \随机信号_5_out ;
  wire [1:0] pull_resistor_2_node, \随机信号_4_out ;
  wire [3:0] \随机信号_2_out , \随机信号_3_out , \随机信号_out ;
  wire [15:0] \_1位加扰A , decoder_3_out0;
  wire [21:0] \_1位加扰 , \_2位加扰 , \_3位加扰 , multiplexer_1_out, multiplexer_2_out, multiplexer_4_out;
  wire [21:6] \_1位加扰B ;
  wire [21:14] multiplexer_3_out;

  Decoder #(.select(4), .enable("false")) decoder_1 (
    .out0(\_1位加扰A [0]), .out1(\_1位加扰A [1]), .out2(\_1位加扰A [2]), .out3(\_1位加扰A [3]), .out4(\_1位加扰A [4]),
    .out5(\_1位加扰A [5]), .out6(\_1位加扰A [6]), .out7(\_1位加扰A [7]), .out8(\_1位加扰A [8]), .out9(\_1位加扰A [9]),
    .out10(\_1位加扰A [10]), .out11(\_1位加扰A [11]), .out12(\_1位加扰A [12]), .out13(\_1位加扰A [13]),
    .out14(\_1位加扰A [14]), .out15(\_1位加扰A [15]), .sel(\随机信号_out ));
  Random #(.width(4)) \u_随机信号  (.clk(CLK), .out(\随机信号_out ));  // open: next, clr
  Random #(.width(4), .seed(18)) \u_随机信号_2  (.clk(CLK), .out(\随机信号_2_out ));  // open: next, clr
  Decoder #(.select(4), .enable("false")) decoder_2 (
    .out0(\_1位加扰B [6]), .out1(\_1位加扰B [7]), .out2(\_1位加扰B [8]), .out3(\_1位加扰B [9]), .out4(\_1位加扰B [10]),
    .out5(\_1位加扰B [11]), .out6(\_1位加扰B [12]), .out7(\_1位加扰B [13]), .out8(\_1位加扰B [14]), .out9(\_1位加扰B [15]),
    .out10(\_1位加扰B [16]), .out11(\_1位加扰B [17]), .out12(\_1位加扰B [18]), .out13(\_1位加扰B [19]),
    .out14(\_1位加扰B [20]), .out15(\_1位加扰B [21]), .sel(\随机信号_2_out ));
  Random #(.width(4), .seed(3)) \u_随机信号_3  (.clk(CLK), .out(\随机信号_3_out ));  // open: next, clr
  Decoder #(.select(4), .enable("false")) decoder_3 (
    .out0(decoder_3_out0[0]), .out1(decoder_3_out0[1]), .out2(decoder_3_out0[2]), .out3(decoder_3_out0[3]),
    .out4(decoder_3_out0[4]), .out5(decoder_3_out0[5]), .out6(decoder_3_out0[6]), .out7(decoder_3_out0[7]),
    .out8(decoder_3_out0[8]), .out9(decoder_3_out0[9]), .out10(decoder_3_out0[10]),
    .out11(decoder_3_out0[11]), .out12(decoder_3_out0[12]), .out13(decoder_3_out0[13]),
    .out14(decoder_3_out0[14]), .out15(decoder_3_out0[15]), .sel(\随机信号_3_out ));
  Random #(.width(2), .seed(21)) \u_随机信号_4  (.clk(CLK), .out(\随机信号_4_out ));  // open: next, clr
  Random #(.width(1), .seed(31)) \u_随机信号_5  (.clk(CLK), .out(\随机信号_5_out ));  // open: next, clr
  Pull_Resistor pull_resistor_1 (.node(pull_resistor_1_node));
  Multiplexer #(.width(22), .enable("false")) multiplexer_1 (
    .in0({\_1位加扰B , {6{1'b0}}}), .in1(\_3位加扰 ), .out(multiplexer_1_out), .sel(pull_resistor_1_node));
  Pull_Resistor #(.pull(1)) pull_resistor_2 (.node(pull_resistor_2_node));
  Multiplexer #(.select(2), .width(22), .enable("false")) multiplexer_2 (
    .in0({22{1'b0}}), .in1({{6{1'b0}}, \_1位加扰A }), .in2(\_2位加扰 ), .in3(multiplexer_1_out),
    .out(multiplexer_2_out), .sel(\随机信号_4_out ));
  Multiplexer #(.select(2), .width(22), .enable("false")) multiplexer_3 (
    .in0({22{1'b0}}), .in1(\_1位加扰 ), .in2(\_2位加扰 ), .in3(multiplexer_2_out),
    .out({multiplexer_3_out, \随机加扰屏蔽字 }), .sel(pull_resistor_2_node));
  not not_1 (not_1_out, comparator_1_eq);
  Comparator #(.width(22), .mode("unsigned")) comparator_1 (
    .a({{6{1'b0}}, \_1位加扰A }), .b({\_1位加扰B , {6{1'b0}}}), .eq(comparator_1_eq));  // open: gt, lt
  Multiplexer #(.width(22), .enable("false")) multiplexer_4 (
    .in0(22'h1), .in1({{6{1'b0}}, \_1位加扰A }), .out(multiplexer_4_out), .sel(not_1_out));
  assign \_2位加扰  = multiplexer_4_out ^ {\_1位加扰B , {6{1'b0}}};  // XOR_Gate xor_1, 22 bits wide
  assign \_3位加扰  = \_2位加扰  ^ {decoder_3_out0, {6{1'b0}}};  // XOR_Gate xor_2, 22 bits wide
  Multiplexer #(.width(22), .enable("false")) multiplexer_5 (
    .in0(multiplexer_4_out), .in1({\_1位加扰B , {6{1'b0}}}), .out(\_1位加扰 ), .sel(\随机信号_5_out ));
  assign \加扰后数据  = \随机加扰屏蔽字  ^ \_14位输入 ;  // XOR_Gate xor_3, 14 bits wide
  // also tied to GND on the sheet: pull_resistor_1_node
  // also tied to VCC on the sheet: {pull_resistor_2_node[0], pull_resistor_2_node[1]}

  // Notes on the sheet:
  //   随机干扰电路
endmodule
