// Logisim project 存储器扩展设计实验.circ as structural Verilog: 3 circuits, main circuit 存储器扩展电路
module \存储器扩展电路  (
  input  [6:0] \区号 ,
  input  [6:0] \位号 ,
  output [31:0] D0,
  output [31:0] D1,
  output [31:0] D6,
  output [31:0] D3,
  output [31:0] D4,
  output [31:0] D5,
  output [31:0] D6_2,
  output [31:0] D7
);

  wire [6:0] multiplier_1_cout, multiplier_1_out, subtractor_1_out;
  wire [13:0] adder_1_out, Addr, bit_extender_1_out;
  wire [31:0] \_4k_32位ROM存储器0_data , \_4k_32位ROM存储器1_data , \_4k_32位ROM存储器2_data , \_4k_32位ROM存储器3_data ;

  Subtractor #(.width(7)) subtractor_1 (.a(\区号 ), .b(7'b0000001), .out(subtractor_1_out));  // open: bin, bout
  ROM #(.addrWidth(14), .dataWidth(32), .Select("low")) \_16k_32位ROM存储器7  (.addr(Addr), .data(D7), .sel(1'b0));
  ROM #(.addrWidth(14), .dataWidth(32), .Select("low")) \_16k_32位ROM存储器6  (.addr(Addr), .data(D6_2), .sel(1'b0));
  ROM #(.addrWidth(14), .dataWidth(32), .Select("low")) \_16k_32位ROM存储器5  (.addr(Addr), .data(D5), .sel(1'b0));
  Multiplier #(.width(7)) multiplier_1 (
    .a(subtractor_1_out), .b(7'b1011110), .out(multiplier_1_out), .cout(multiplier_1_cout));  // open: cin
  assign bit_extender_1_out = {{7{1'b0}}, \位号 };  // Bit_Extender bit_extender_1
  ROM #(.addrWidth(14), .dataWidth(32), .Select("low")) \_16k_32位ROM存储器4  (.addr(Addr), .data(D4), .sel(1'b0));
  ROM #(.addrWidth(14), .dataWidth(32), .Select("low")) \_16k_32位ROM存储器3  (.addr(Addr), .data(D3), .sel(1'b0));
  ROM #(.addrWidth(14), .dataWidth(32), .Select("low")) \_16k_32位ROM存储器2  (.addr(Addr), .data(D6), .sel(1'b0));
  ROM #(.addrWidth(14), .dataWidth(32), .Select("low")) \_16k_32位ROM存储器0  (.data(D0), .sel(1'b0));  // open: addr
  Adder #(.width(14)) adder_1 (
    .a({multiplier_1_cout, multiplier_1_out}), .b(bit_extender_1_out), .out(adder_1_out));  // open: cin, cout
  Subtractor #(.width(14)) subtractor_2 (.a(adder_1_out), .b(14'h1), .out(Addr));  // open: bin, bout
  ROM #(.addrWidth(12), .dataWidth(32), .Select("low")) \_4k_32位ROM存储器0  (
    .addr(Addr[11:0]), .data(\_4k_32位ROM存储器0_data ), .sel(1'b0));
  ROM #(.addrWidth(12), .dataWidth(32), .Select("low")) \_4k_32位ROM存储器1  (
    .addr(Addr[11:0]), .data(\_4k_32位ROM存储器1_data ), .sel(1'b0));
  ROM #(.addrWidth(12), .dataWidth(32), .Select("low")) \_4k_32位ROM存储器2  (
    .addr(Addr[11:0]), .data(\_4k_32位ROM存储器2_data ), .sel(1'b0));
  ROM #(.addrWidth(12), .dataWidth(32), .Select("low")) \_4k_32位ROM存储器3  (
    .addr(Addr[11:0]), .data(\_4k_32位ROM存储器3_data ), .sel(1'b0));
  Multiplexer #(.select(2), .width(32), .enable("false")) multiplexer_1 (
    .in0(\_4k_32位ROM存储器0_data ), .in1(\_4k_32位ROM存储器1_data ), .in2(\_4k_32位ROM存储器2_data ),
    .in3(\_4k_32位ROM存储器3_data ), .out(D1), .sel(Addr[13:12]));

  // Other names for the same wires on the sheet: D2[31:0] = D6; D6_t[31:0] = D6_2

  // Notes on the sheet:
  //   输入引脚区
  //   contents of _16k_32位ROM存储器7 (hex, n*v repeats v):
  //   0 0 3000 0 0 80 5*0 240 5*0 c 1800 7*0 1ff0 9*0 80 0 0 7f0 1004 c0 0 400 4*0 3e0 7*0 200 20c 0 60018
  //   30000c00 10*0 21c2 400 430 0 1c0 605e 2002 2002 0 0 3e0 80 80 7*0 80 80 3ffc 16*0 7b0 8*0 3ce6 1ef6
  //   9*0 9*808 11*1008 10*3e0 0 0 10*1008 23*0 4 2000 17*0 2000 c 0 3000 180 17*0 300048 9*0 7f8 2 ff0
  //   9*0 7800cc0 0 0 780 5*0 f000600 780030 7*0 18000400 0 c0 800080 180 0 40 20 0 0 0 200 6*0 e0 e0 4*40
  //   0 0 e0 e0 0 0 200 200 0 0 70 70 2000 2000 40 40 5*0 3c0 3c0 2060 4*0 80 80 80 180 180 180 6*0 80 80
  //   80 c00 0 be0 0 40 20 30 80 c0 0 380 180 100 60 0 20 0 0 20 90 3e0 13*0 1000 0 80 0 100 0 0 0 10 2040
  //   2040 0 0 1000 1000 4*0 80 80 1800 1800 4*0 800 800 4*1000 0 0 0 1000 1000 200 200 1000 0 1000 80
  //   27*0 800 400 2040 0 0 0 100 0 0 0 1800 100 47*0 80 8 6*0 80 54*0 1ff8 0 0 0 1e3c 9*0 c00 0 0 2 101*0
  //   7c0 4*0 4000a0 3000 0 0 4020a0 0 4000a0 20201050 220 4000a0 8000 200020 40 100 0 1000100 80004000 0
  //   4000400 1000080 0 1000100 0 fe0 0 1020 18 0 800 40 20 607c 0 607c 1000100 6000 27*0 1000100 1800180
  //   8*0 1000100 1000100 1800180 1800180 1000100 1000100 1800180 1800180 8*0 1000100 1000100 1000100
  //   1800180 1800180 1000100 1800180 1800180 1000100 1000100 1000100 1800180 1800180 1000100 1800180
  //   1800180 4*1000100 4*1800180 8*0 5*1000100 1800180 1800180 1000100 1000100 1800180 1800180 1000100
  //   4*1800180 22*0 8 1000 0 0 1000 0 1800 11*0 600 18000c00 c 0 3000 180 17*0 e00110 9*0 7f8 2 ff0 8*0
  //   c001200 78008c0 0 0 700 5*0 1e000c00 f00060 7*0 78008c0 0 30 800080 600 8*0 8 1000 0 0 1000 0 1800
  //   11*0 600 18000c00 c 0 3000 180 17*0 e00110 9*0 7f8 2 ff0 8*0 c001200 78008c0 0 0 700 5*0 1e000c00
  //   f00060 7*0 78008c0 0 30 800080 600 0 4*ff0300c ff0381c ff0381c ff0300c ff03b1c ff03ffc df03efc
  //   ff03f1c ff03e7c ff03ffc ff03efc 80019ff9 7ffe6006 7ffe6006 8001bffd fff0603 ffb07fb f000f9fa
  //   f802fc02 1ff88181 e0077e7e e0077e7e 1ff88181 1ff8 ffffe007 1ff8 ffffe007 7ffe7ffe 9ff98001 7ffe6006
  //   9ff98001 0 ffffffff 1ff8 0 ff003c0 180 ff0381c ff03ffc 0 0 0 1800180 ff0 3c0 c0 3c0 3c0 300 4*0 7ffe
  //   ffff8001 0 600060 20006 6000600 40006000 700070 7e e000e00 7e00 c000c0 c001c00 3800380 fffe 300c300c
  //   300c 18001800 0 ffffffff ffffffff ffffffff ffff8000 ffff0001 ffff0000 1ff81008 18002400 780 1e0 ffff
  //   ffff0000 1000100 3800 6*0 6000780 0 2000380 30003c0 0 0 78003c0 0 4000e0 0 8800d80 1800780 0 0
  //   48007c0 0 1800180 0 1800180 1800180 0 0 1800180 0 1800180 0 18007e0 18005a0 0 0 3c007e0 0 1e003f00 0
  //   78007c 1e003700 0 0 780058 0 7f00be 80c0d3c0 7001f00 1ee03fc 8000 20002 f00ff80 0 1000180 0 981eb8
  //   19001f00 0 0 900fb8 0 400240 0 2000240 2000ee0 0 0 400720 0 c000e0 1f803fee 3007680 18003c0 0 0
  //   3100130 0 10003e 7b38 1e001f00 3800e0 0 0 1c18033c 0 2000200 0 400040 2000600 0 0 400040 0 1800040 0
  //   1800040 18000c0 0 0 0 70 c 4000 40084014 2000 0 80 1000100 0 0 1800 0 0 100 0 0 180 0 7ffc 0 380 0 0
  //   0 6004100e 0 7e00 20*0 1800180 3010301 80c080c0 1 8000 5*0 c000c000 ffffffff 30003 ffffffff c000c000
  //   30003 0 ffffffff 0 ffffffff 80008000 ffff8000 10001 ffff0001 80008000 10001 0 ffff0000 111*0 80c0814
  //   40104028 604010e 2604510e 404020e 604010e 4000604 fe 40447fc 813d4 6088198 c004300e 200050 c08221c
  //   40004ffe 1304108c 3044098a 30100c30 103e1042 2304508c 20803f8 808080 904948c 1006108 800960e 800080
  //   fffe 4004 204890e 40042244 10881154 1404120e 20842046 6008181c 1c04120e 2c04220e ffc 20085894
  //   20005804 10000804 1fe 1ffe 4004 43fe 1ffe 2304588e 304c88e 100010fe 200050fe 100010fe 3020086
  //   9180888 81ff8 ffc1004 2008 110411fc 10101ff0 200457fc 120813f8 82004504 40202020 10201020 48fe
  //   80044fe 4142b2a4 20005904 85044a8e 83024c86 10001904 8008904 24105228 20405040 10401040 89008
  //   1000100 2040 204020 404040 1001120 10201420 14101228 1a108928 200420 10401040 2102528 204020 2101128
  //   14201250 4202250 7fc 80094fe ffc 408665c 10082814 20302110 7fc0804 10401844 fffe 20fe 7ffc 200050fe
  //   21005104 3001110 10102828 2000707e c08248 10401040 202420 ff0 1000100 447e 1000100 10201050 30080818
  //   2021106 120813f8 22025106 10101ff0 47f42894 20883f8 1304188e 20201020 1000100 1000100 1000100
  //   85104aa8 11084a94 81104128 3006104 9cc44a4 8ffc 8ffc 1840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
  //   contents of _16k_32位ROM存储器6 (hex, n*v repeats v):
  //   0 c000c00 48004800 0 0 1c00140 0 11001100 4000e0 0 0 2400240 5*0 380060 e000300 400080 200 240 240
  //   1000100 f800080 3800280 10101fd0 ff00820 7f80208 7f007e0 7f003f0 ff8 808 180 180 2002 1400220
  //   1ffc1ffc 3c3c1818 c18180c 10041004 3000400 1818 c002e00 1ffc0080 4800480 0 0 c181004 c001200 c001200
  //   5*0 2000200 23002c0 18200620 600186 30030c0 0 180 1818 1c00220 800080 0 0 0 1e00310 8003c0 16340808
  //   3e00610 a7809c8 418c2252 2200020 60c010cc 180c1634 180c1e3c 3c00c30 3c00ff0 c1811c4 1400220 1c003e0
  //   3ffc2004 3ffc3ffc 7fff2002 7fff3ffe 1188 0 0 800080 1c001c0 3ffc3ffc 16*0 3300300 1fec0c2c 78c0ccc
  //   3cc018c 78c0ecc 78c0ccc 60c060c 78c0ccc 78c0ccc 19b61b18 c660c60 7bf63316 79c63360 78f63066 78e631b6
  //   78e631b6 78c630c6 78e631b6 78e631b6 fcf3c59b 100413c4 10041004 100411c4 100411e4 100411c4 100411c4
  //   11841184 100411c4 100411c4 20042e64 20042e74 20042ef4 20042e64 20042e74 20042e64 20042e64 20042e44
  //   20042e64 20042e64 20042f24 c181004 c181004 c1811c4 c1811e4 c1811c4 c1811c4 c181184 c1811c4 c1811c4
  //   c181004 0 0 20042004 20042004 20042004 20042814 20042004 20042814 200420f4 20042014 20042874
  //   20842084 0 1ff8 1c00080 7700220 1ddc0888 1c200820 800080 21c0208 43e0414 4fe0454 1ddc0888 e380410
  //   1ddc0888 3bfc1128 7d8 0 1800180 0 2200220 3c00180 1018 f1e18f0 0 80010 10000800 808 80 20001000 0
  //   30003000 20001000 3e00630 3c00180 ff00610 3c00660 1e000c0 3c00660 3c00660 3000300 3c00660 3c00660
  //   30003000 10001800 3000c0 0 c000300 3c00180 3f00408 1c3c0818 1fe00c38 3e00630 1fc00c70 1ff80c18
  //   1e000c00 3f00618 1e3c0c18 3c00180 f8018c0 1e1e0c1c 1ff80c18 381e108c 1c100830 3e00630 1e000c00
  //   4003f0 1e1c0c38 17c01c30 3c00180 3e00630 1000380 6100630 1c3c0818 3c00180 3ff83018 6000600 6000c
  //   300030 0 3ffc0000 0 7d8 bf0 7e0 7d0 7e0 3c0 18601ce0 e78 3c0 cc00cc0 e3c 3c0 3def 1e78 3e0 60007e0
  //   300030 f00 3e0 e0 7d8 80 210 3e7c 2000100 7f0 1000100 800080 400040 0 200810 100e08 100 2000500
  //   2000100 1000080 870 107c08c4 400 4000c20 11000880 11000880 3000420 3000420 c00180 c00180 4200610
  //   4200610 7f0 7f0 3000420 3000420 1c00320 1c00320 1000080 1000080 1f80200 1f80200 800100 800100
  //   303c1040 303c1040 300018 300018 0 100 100 e00130 e00130 4600800 4600800 30941138 8780c8c 1036
  //   8005836 400820 9441538 9441538 9441538 6600810 6600810 6600810 801144 801144 801144 0 0 0 9441538
  //   9441538 9441538 136009c0 211850b0 6100408 400820 a00110 300060 7800c0 400420 830140c 1800258 4580470
  //   700018 800040 900128 8085814 100008 400 4000c20 10502888 154c0a28 4100880 10081014 11*0 800 8000400
  //   100 800080 100 800040 0 0 20 301050 10a00810 10a00810 200020 200020 8000400 8000400 10000800
  //   10000800 0 0 400020 400020 c000200 c000200 1004 1004 3f0 3f0 4000200 4000200 4*8000400 400 10000800
  //   10000800 8000400 8000400 2000200 2000200 8000400 0 8000400 800080 4*0 1f0 1f0 1f0 10000800 10000800
  //   10000800 4 4 4 800180 800180 800180 40 18 2 10000800 f8 40 800080 0 0 0 1ffc0004 4000200 2000100
  //   10601050 c000600 ffc 100 800040 800080 0 10000800 c000200 800040 0 400 8*0 1c3c0818 1fe00e30
  //   1e000c00 1ffc0818 1ff80e18 3ff83018 1e3c0c18 3e00630 3c00180 1e3c0c18 1c3c0818 381e108c 1c1c0838
  //   ff80ff8 3e00630 1e3c0c18 1e000c00 ff80ff8 3c0 3c00180 3c00180 1c3c0818 3c00180 1f7c1f7c 8*0 620
  //   60006c0 800080 3c00660 3c0 1e00010 180018 1c00360 8001c0 400 410 80809dc 80 1e00010 0 860 c00 0
  //   8001c0 18003e0 1000100 810 1000100 39*0 1c3c0818 1fe00e30 1fe00e30 1e000c00 20043ffc 1ff80e18
  //   e180c08 7bde318c 1e00670 1e3c0c18 c180e18 1e1e0c18 30783830 381e108c 1e3c0c18 3e00630 1e3c0c18
  //   1e000c00 3e00630 3c0 1e000900 3c00180 1c3c0818 1ffe0c18 3c0018 7ffe318c 17fff fe00730 3f3c1d98
  //   fe00730 3e00630 3cf8198c 3c3c1818 15*0 390 1c00360 fe0 f00 0 0 1e0 0 3c0 0 f78 6*0 f00 0 0 400
  //   3c00180 e78 8 78 0 4 fe0 1fbc fe0 3c0 1e70 c78 44*0 8200820 4*0 1100010 c100310 0 1ffc1000 11100810
  //   81ff0 1100010 8100408 2200440 200010 40002000 200020 400080 1000100 7ffc0100 1000100 20002000
  //   fe00820 4000400 400020 103ff0 1000100 fe01010 10102008 7f00800 8100410 200040 101ff0 4000220 200010
  //   100010 10800880 3ff8 10840884 1000100 18000410 8 26*0 1000100 1800180 8*0 1000100 1000100 1800180
  //   1800180 10001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
  //   contents of _16k_32位ROM存储器5 (hex, n*v repeats v):
  //   0 18002000 30000000 0 0 2200220 0 8800880 c001c0 0 38 2400240 5*0 400040 1000100 1000200 1000080
  //   2400480 2400120 1000100 800080 2800280 500050 8400880 1080088 7c00780 1f000f0 80 4100220 1800000
  //   1800000 20021004 2200410 8040400 18181818 10041004 10041004 4000800 18180000 3b001080 800080 4800480
  //   1ff80800 0 20022002 1000100 1000100 0 3ffc0000 70 c18 c1c 1001ffc 3000e00 1a00060 6181860 c30030c
  //   c18 3c003c0 3c3c3c3c 2200220 800080 0 0 0 6080c00 cb01898 10041004 a081900 7800100 12520a52 400080
  //   11d21152 9480888 f780ff8 10081008 1ff81ff8 2632280a 4100808 7f00ff8 20042004 3ffc3ffc 10041004
  //   1ffc1ffc 9900420 40 100 800080 3e003e0 3ffc0000 16*0 3000300 6200300 18600060 1803fe0 18600060
  //   18601860 6000600 18601860 18600060 1b181b18 c600c60 31103180 36303030 306037f8 33183018 33183318
  //   30c030c0 33183318 33183018 c5986198 21822182 27f22312 23622632 20c220c2 23622632 23622632 21822182
  //   23622632 23622632 44924492 44224422 44924442 44924492 44224422 44924492 44924492 44424442 44924492
  //   44924492 49524852 21e220c2 27f22312 23622632 20c220c2 23622632 23622632 21822182 23622632 23622632
  //   2f7226da 0 0 40024002 5ffa4012 5ffa4012 4ff24812 5ffa4222 48124822 410a4102 48124432 44524252
  //   40824082 0 10081008 800080 2200220 8880888 8500850 1400140 5080508 a140a14 a540a54 8880850 4100220
  //   8880888 11280a28 c700c30 0 0 0 2200ff8 1800ff0 8240424 10601870 0 200020 4000400 4100220 800080
  //   18001800 0 0 8000400 c180c18 1800180 3100180 c300030 c01ff0 c300030 c300c30 3000300 c300c30 c300030
  //   0 18000000 3000c00 0 c00030 0 80011cc 8180c38 c0c0c0c c081800 c180c0c c080c00 c000c00 c181818
  //   c180c18 1800180 38c000c0 c380c70 c080c00 108c11cc 8700870 c18180c c000c00 6580d4c c300c70 10180018
  //   1800180 c180c08 2800640 6280d68 4300660 1800180 18080c00 6000600 180030 300030 0 0 0 c600c60 6180618
  //   c300c00 c600c60 c300c00 1800180 f800c00 6300630 1800180 c000c0 6300760 1800180 18c618c6 c300c30
  //   6300630 6180618 3f00630 6000600 6300030 1900190 c700c30 1c00340 6300528 c300360 1800340 6100300
  //   1000100 800080 400040 38 16881108 11440884 2800200 4800c00 c00060 600030 4c80280 4800280 c601490
  //   14500c88 888044c 888044c 4d00320 4d00320 3000200 3000200 5100c10 5100c10 c381000 c381000 4c00330
  //   4c00330 6100408 6100408 400140 400140 2000240 2000240 1000100 1000100 18800c80 18800c80 c018c c018c
  //   800060 c00030 c00030 2000200 2000200 8000800 8000800 18d00c10 12001000 294c2a38 284c1838 14101208
  //   10e01010 10e01010 10e01010 10081008 10081008 10081008 3a4e0658 3a4e0658 3a4e0658 e0038 e0038 e0038
  //   10e01010 10e01010 10e01010 6800080 506049a0 4080c08 14101248 1080108 800110 800118 e700aa8 126210a2
  //   42003a0 3a00020 80398 400020 18c40c04 28221820 180c0c04 c201410 14100c08 4868280c 4100300 4800380
  //   8200820 11*0 4000200 2000200 1000100 800080 800040 200010 1ffc 3ffe0080 86004a0 8100410 4100410
  //   4100410 400040 400040 2000100 2000100 4000200 4000200 3ffc0008 3ffc0008 200020 200020 1000080
  //   1000080 8080410 8080410 2000200 2000200 1000080 1000080 2200140 2200140 2000100 2000100 2000100
  //   4000200 4000200 2000100 2000100 2000200 2000200 2000100 3ffe 2200140 20801080 10000800 2000 2000
  //   2000 2000200 2000200 2000200 4000200 4000200 4000200 80010 80010 80010 2802082 2802082 2802082
  //   800100 1e00e00 1ff40808 4000220 800080 400040 800100 0 3ffe 7f00010 40004 1000080 800040 8480844
  //   5000480 8040804 800040 200010 800080 3ffe0080 4000200 1000080 200010 4100228 2000100 8*0 8180818
  //   c180c18 c000c00 8180818 c080c00 18080c00 c180c18 c18180c 1800180 c380c70 8180818 108c11cc 8680868
  //   8080000 c18180c c180c18 c000c00 8080c00 1800180 1800180 ff01998 4300660 1800180 11440760 8*0 d5018c0
  //   7e00630 800080 c300c30 6600c30 1e00600 180618 6300630 3200300 6780630 4180228 b740e30 c001c0 600180
  //   1c00360 1cd00248 c000c00 1c00360 3200300 7300618 3800d60 4180228 3800d60 4100e38 38*0 8180818
  //   c180c18 c180c18 c000c00 8300830 c080c00 c000c00 19981998 838101c e180d18 d180d18 c380c70 28300830
  //   108c11cc c180c18 c18180c c180c18 c000c00 c081800 1800180 8001c0 ff01998 4300660 c180c18 180018
  //   318c318c 318c318c 6180618 18d818d8 6180618 818000c 1b061b06 c180618 15*0 6d80c68 6300630 6300630
  //   60006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
  //   contents of _16k_32位ROM存储器4 (hex, n*v repeats v):
  //   0 0 0 180 0 4100410 c30 4400440 2600030 0 fe61c3 2400240 318c 4*0 400040 1000100 4000800 400020
  //   4800900 1200090 1000100 800080 2800280 500050 8800900 880048 7800700 f00070 800080 1400080 1ff8 0
  //   10040808 4100808 4000200 18181818 10041004 10041004 8000fc0 0 800040 800080 2400240 4000200 20022002
  //   408141c1 1000100 3800540 1ffc0000 3ffc0000 20881104 12042102 12202140 1000080 32006200 380026
  //   21800600 c20030 12242142 1800000 18180000 1c00080 800ff8 0 1000100 4800480 c000c00 9800b0 20022002
  //   19001900 1800180 58c0200 1400220 1352134c 4100808 7f00ff8 20042004 3ffc3ffc 48095005 10042002
  //   1ffc3ffe 20042004 3ffc3ffc 8080808 ff80ff8 2401998 30003c 6001e00 800080 4900080 17*0 3000300
  //   18000c0 6000c0 31801980 600060 18601860 3000300 18600cc0 7e00ce0 1b181b18 c600c60 30c03060 30303060
  //   36603360 30183018 33183318 30403040 331831b0 30f831b8 31981998 21822182 218220c2 20322062 2ff228c2
  //   20322032 26322732 20c22062 26322362 203221f2 44924492 44224422 44424422 44124412 45f24522 44124412
  //   44924492 44224422 44924492 44124412 44524452 40c140c1 418140c1 40314061 4ff144c1 40314031 46314731
  //   40c14061 46314361 40b14371 46d946d9 0 0 40024002 40024002 40024002 4c724a52 42224222 44224462
  //   41024102 44224222 42424242 40824082 0 10080000 800080 2200220 8880888 8500888 3200220 5080508
  //   a140a14 a540a54 8500820 2200140 5080208 a280428 c300c30 0 1800180 0 ff80220 1800180 2180100 cd8058c
  //   0 400040 2000200 1401ffc 800080 0 0 0 2000100 c180c18 1800180 c00060 300060 18c00cc0 300030 c300c30
  //   1800180 c300660 3f00670 30003000 1800 30006000 1ff80000 c0006 8000c0 12341224 7f00430 c0c0c18
  //   18001800 c0c0c0c c000c20 c000c20 183c1800 c180c18 1800180 c000c0 ce00dc0 c000c00 114c134c 8d008d0
  //   180c180c c000fe0 188c180c cc00fe0 180030 1800180 c080c08 6400c20 d680d68 36001c0 1800180 6000300
  //   6000600 6000c0 300030 1004 0 0 7e00060 6180618 c000c00 c600c60 ff00c30 1800180 7800cc0 6300630
  //   1800180 c000c0 7c00660 1800180 18c618c6 c300c30 6300630 6180618 6300630 6000600 1e00300 1800180
  //   c300c30 6200c10 d6808cc 1c00360 3200610 1800060 1000200 0 400020 fe61c3 9b00540 9480550 4000400
  //   8000800 100030 100018 1000080 1000080 c080608 6040504 4440244 4440244 200040 200040 4000c00 4000c00
  //   8100810 8100810 10000000 10000000 200040 200040 4000400 4000400 2800280 2800280 2a00220 2a00220
  //   1c800b80 1c800b80 4000400 4000400 c800b0 c800b0 100008 80008 80008 1000100 1000100 4000300 4000300
  //   4100420 10001000 14040a04 18082c04 12082104 6*10100810 1e00080 1e00080 1e00080 e01180 e01180 e01180
  //   10100810 10100810 10100810 800080 2e201430 16081608 22882104 1c80308 1280604 1240e02 9240924
  //   11221122 400040 400040 2f00200 4200e20 6040388 18202c20 60c0388 c080608 6040504 18040c0c 800140
  //   c019b0 4200620 11*0 2000100 1000180 1000100 800080 200010 100008 800080 800080 2200120 2100110
  //   2080208 2080208 fc000f8 fc000f8 800040 800040 1000080 1000080 80008 80008 2200220 2200220 400020
  //   400020 2200140 2200140 2000200 2000200 400020 400020 800140 800140 1000080 1000080 800040 4*1000080
  //   2000220 2000220 1000080 0 800140 8880490 4000200 10040808 10040808 10040808 2000200 2000200 2000200
  //   1000080 1000080 1000080 201040 201040 201040 10840888 10840888 10840888 2800040 10000000 4100200
  //   1400080 803ffc 800080 1000100 1ff80020 20 100010 40004 400020 4400440 4400440 4400420 8040804 200010
  //   100008 3ffe0880 800080 1000080 400020 100008 1080108 800080 8*0 43007f0 c380c70 c000c00 4300430
  //   c000c20 6000300 c180c18 1a2c1bec 1800180 ce00dc0 4300430 114c134c 8c808c8 41007f0 180c180c c180c18
  //   c000fe0 6000300 1800180 1800180 318c318c 36001c0 18003c0 e301c18 8*0 18c018c0 63006e0 1c00120
  //   c300660 c200600 8000800 6180618 6300630 3000300 66006c0 2200140 c300c30 1200320 2000200 6300630
  //   2400240 d800f60 6300630 3000300 6080608 19303118 2200140 19301110 1d5c194c 38*0 43007f0 c380c70
  //   c380c70 c000c00 8300430 c000c20 c200fe0 db00ff0 380070 d180c98 c980c98 c600cc0 8300430 114c134c
  //   c180c18 180c180c c180c18 c000fe0 18001800 1800180 3600320 318c318c 36001c0 c180c18 3d80678 318c318c
  //   318c318c 6180730 18d81d98 6180730 c000c 1b061b06 31803d8 15*0 c2006e0 6300630 6300660 6000600
  //   8600460 6080c00 40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
  //   contents of _16k_32位ROM存储器3 (hex, n*v repeats v):
  //   0 0 0 1800000 7f00000 8080808 c300000 6600330 10300c18 7ffe0000 3f800e00 2400240 318c0000 4*0 400040
  //   1000100 4000200 100020 9000480 900120 1000100 800080 2800280 500050 9000880 480088 7000780 7000f0
  //   800ff8 1400220 0 0 8080410 8081004 3000300 18181818 10041004 10041004 8000800 0 400020 800080
  //   2400240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
  //   contents of _16k_32位ROM存储器2 (hex, n*v repeats v):
  //   5*0 10041004 0 3300110 ffc0608 0 0 2400240 0 300030 10000800 cc00cc 44002200 400040 1000100 1000080
  //   400080 4800240 1200240 1000100 800080 28002f8 500050 8800840 880108 78007c0 f001f0 800080 4100808
  //   1800180 1800180 4100220 10042002 6000c04 18181818 10041004 10041004 4000400 1818 200010 800080
  //   1200120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
  //   contents of _16k_32位ROM存储器0 (hex, n*v repeats v):
  //   8*0 1000000 0 0 2400000 5*0 c0000 18000000 16*0 800000 0 0 0 10040000 7f00000 0 0 80000 800000 0 0 0
  //   c1803e0 0 600000 5*0 200000 0 18200000 180006 c003000 0 0 0 800000 1c00000 1c00000 200000 900000
  //   48003000 0 0 500000 0 40000 1c00000 38300000 800080 800080 3c00000 3c00000 c1803e0 1400080 1c00080 0
  //   0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
  //   存储器扩展电路
  //   输出引脚区
  //   contents of _4k_32位ROM存储器0 (hex, n*v repeats v):
  //   7*0 1100000 3000380 0 0 2400240 0 100008 c000c00 440022 33003300 600038 3000e00 400000 1000200
  //   2400000 2400000 10001f0 800080 20803f8 500070 8200ff0 20807f8 7e007f0 3f007f0 800080 0 0 0 2200140
  //   20020000 18041ffc 18183ffc 10041004 180c0c18 30000c0 18180000 100008 800080 1200120 100008 63001c0
  //   2002100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
  //   contents of _4k_32位ROM存储器1 (hex, n*v repeats v):
  //   280fffe 53fc5048 420fffe 4bfc4950 11001ffe 2007ffc 13f810a0 21242124 45084508 43f838a0 11081108
  //   3e442220 448845fc 48887dfc 20881080 8207efc 57fe7840 11081108 17f830a0 7f241424 20082008 1000100
  //   841080 104817fe 21082108 888f888 104017c0 10441040 4bfe4894 10a010a0 24401820 11083108 48a048a0
  //   44a044a0 54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
  //   contents of _4k_32位ROM存储器2 (hex, n*v repeats v):
  //   3933*0 27fc4048 28881080 8c8147e 3ec8087e 23f84090 20fe3f28 efee1830 48503c50 48043c20 48443c50
  //   48203dfc 487c3c48 48403c7e 48203de0 48883c48 7ffe4940 48883c40 48203dfc 4bfe3c24 4bfe3c44 48203c20
  //   4bfe3c04 4bfe3c04 2003ff8 48043c04 48243c20 48043c00 4afe3c24 49623d7e 49443de4 48883c7c 48403c40
  //   253a40a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
  //   存储器地址A（14位）
endmodule

module \存储器扩展测试电路  (
  input  CLR
);

  wire CLK_out;
  wire [7:0] counter_1_q;
  wire [15:0] adder_1_out, rom_1_data;
  wire [31:0] \存储器扩展电路_1_d0 , \存储器扩展电路_1_d1 , \存储器扩展电路_1_d3 , \存储器扩展电路_1_d4 , \存储器扩展电路_1_d5 , \存储器扩展电路_1_d6 ,
       \存储器扩展电路_1_d6_2 , \存储器扩展电路_1_d7 , \汉字字库电路_1_d0 , \汉字字库电路_1_d1 , \汉字字库电路_1_d3 , \汉字字库电路_1_d4 ,
       \汉字字库电路_1_d5 , \汉字字库电路_1_d6 , \汉字字库电路_1_d6_2 , \汉字字库电路_1_d7 ;

  Counter #(.behavior("old")) counter_1 (
    .Q(counter_1_q), .clk(CLK_out), .clr(CLR));  // open: load, D, count, carry, preset
  Clock CLK (.out(CLK_out));
  ROM #(.dataWidth(16), .Select("high")) rom_1 (.addr(counter_1_q), .data(rom_1_data));
  Adder #(.width(16)) adder_1 (.a(rom_1_data), .b(16'h5f60), .out(adder_1_out));  // open: cin, cout
  \存储器扩展电路  \u_存储器扩展电路_1  (
    .D0(\存储器扩展电路_1_d0 ), .D1(\存储器扩展电路_1_d1 ), .D6(\存储器扩展电路_1_d6 ), .D3(\存储器扩展电路_1_d3 ),
    .\区号 (adder_1_out[14:8]), .\位号 (adder_1_out[6:0]), .D4(\存储器扩展电路_1_d4 ), .D5(\存储器扩展电路_1_d5 ),
    .D6_2(\存储器扩展电路_1_d6_2 ), .D7(\存储器扩展电路_1_d7 ));
  \汉字字库电路  \u_汉字字库电路_1  (
    .D0(\汉字字库电路_1_d0 ), .D1(\汉字字库电路_1_d1 ), .D6(\汉字字库电路_1_d6 ), .D3(\汉字字库电路_1_d3 ), .\区号 (adder_1_out[14:8]),
    .\位号 (adder_1_out[6:0]), .D4(\汉字字库电路_1_d4 ), .D5(\汉字字库电路_1_d5 ), .D6_2(\汉字字库电路_1_d6_2 ),
    .D7(\汉字字库电路_1_d7 ));
  DotMatrix #(.inputtype("row"), .matrixcols(16), .matrixrows(16), .dotshape("circle")) dotmatrix_1 (
    .row0(\存储器扩展电路_1_d0 [15:0]), .row1(\存储器扩展电路_1_d0 [31:16]), .row2(\存储器扩展电路_1_d1 [15:0]),
    .row3(\存储器扩展电路_1_d1 [31:16]), .row4(\存储器扩展电路_1_d6 [15:0]), .row5(\存储器扩展电路_1_d6 [31:16]),
    .row6(\存储器扩展电路_1_d3 [15:0]), .row7(\存储器扩展电路_1_d3 [31:16]), .row8(\存储器扩展电路_1_d4 [15:0]),
    .row9(\存储器扩展电路_1_d4 [31:16]), .row10(\存储器扩展电路_1_d5 [15:0]), .row11(\存储器扩展电路_1_d5 [31:16]),
    .row12(\存储器扩展电路_1_d6_2 [15:0]), .row13(\存储器扩展电路_1_d6_2 [31:16]), .row14(\存储器扩展电路_1_d7 [15:0]),
    .row15(\存储器扩展电路_1_d7 [31:16]));
  DotMatrix #(.inputtype("row"), .matrixcols(16), .matrixrows(16), .dotshape("circle")) dotmatrix_2 (
    .row0(\汉字字库电路_1_d0 [15:0]), .row1(\汉字字库电路_1_d0 [31:16]), .row2(\汉字字库电路_1_d1 [15:0]),
    .row3(\汉字字库电路_1_d1 [31:16]), .row4(\汉字字库电路_1_d6 [15:0]), .row5(\汉字字库电路_1_d6 [31:16]),
    .row6(\汉字字库电路_1_d3 [15:0]), .row7(\汉字字库电路_1_d3 [31:16]), .row8(\汉字字库电路_1_d4 [15:0]),
    .row9(\汉字字库电路_1_d4 [31:16]), .row10(\汉字字库电路_1_d5 [15:0]), .row11(\汉字字库电路_1_d5 [31:16]),
    .row12(\汉字字库电路_1_d6_2 [15:0]), .row13(\汉字字库电路_1_d6_2 [31:16]), .row14(\汉字字库电路_1_d7 [15:0]),
    .row15(\汉字字库电路_1_d7 [31:16]));

  // Notes on the sheet:
  //   GB2312
  //   contents of rom_1 (hex, n*v repeats v):
  //   bbaa d6d0 bfc6 bcbc b4f3 d1a7 cac7 b9fa bcd2 bdcc d3fd b2bf d6b1 caf4 b5c4 c8ab b9fa d6d8 b5e3 b4f3
  //   d1a7 a3ac d3c9 d4ad bbaa d6d0 c0ed b9a4 b4f3 d1a7 a1a2 cdac bcc3 d2bd bfc6 b4f3 d1a7 a1a2 cee4 baba
  //   b3c7 cad0 bda8 c9e8 d1a7 d4ba d3da a3b2 a3b0 a3b0 a3b0 c4ea a3b5 d4c2 a3b2 a3b6 c8d5 bacf b2a2 b3c9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
  //   存储器扩展测试电路
  //   标准库
endmodule

module \汉字字库电路  (
  input  [6:0] \区号 ,
  input  [6:0] \位号 ,
  output [31:0] D0,
  output [31:0] D1,
  output [31:0] D6,
  output [31:0] D3,
  output [31:0] D4,
  output [31:0] D5,
  output [31:0] D6_2,
  output [31:0] D7
);

  wire [6:0] multiplier_1_cout, multiplier_1_out, subtractor_1_out;
  wire [13:0] adder_1_out, bit_extender_1_out, subtractor_2_out;

  ROM #(.addrWidth(14), .dataWidth(32), .Select("high")) rom_1 (.addr(subtractor_2_out), .data(D0));
  ROM #(.addrWidth(14), .dataWidth(32), .Select("high")) rom_2 (.addr(subtractor_2_out), .data(D4));
  Subtractor #(.width(7)) subtractor_1 (.a(\区号 ), .b(7'b0000001), .out(subtractor_1_out));  // open: bin, bout
  Multiplier #(.width(7)) multiplier_1 (
    .a(subtractor_1_out), .b(7'b1011110), .out(multiplier_1_out), .cout(multiplier_1_cout));  // open: cin
  ROM #(.addrWidth(14), .dataWidth(32), .Select("high")) rom_3 (.addr(subtractor_2_out), .data(D1));
  ROM #(.addrWidth(14), .dataWidth(32), .Select("high")) rom_4 (.addr(subtractor_2_out), .data(D5));
  Adder #(.width(14)) adder_1 (
    .a({multiplier_1_cout, multiplier_1_out}), .b(bit_extender_1_out), .out(adder_1_out));  // open: cin, cout
  assign bit_extender_1_out = {{7{1'b0}}, \位号 };  // Bit_Extender bit_extender_1
  ROM #(.addrWidth(14), .dataWidth(32), .Select("high")) rom_5 (.addr(subtractor_2_out), .data(D6));
  ROM #(.addrWidth(14), .dataWidth(32), .Select("high")) rom_6 (.addr(subtractor_2_out), .data(D6_2));
  Subtractor #(.width(14)) subtractor_2 (.a(adder_1_out), .b(14'h1), .out(subtractor_2_out));  // open: bin, bout
  DotMatrix #(.inputtype("row"), .matrixcols(16), .matrixrows(16), .dotshape("circle")) dotmatrix_1 (
    .row0(D0[15:0]), .row1(D0[31:16]), .row2(D1[15:0]), .row3(D1[31:16]), .row4(D6[15:0]), .row5(D6[31:16]),
    .row6(D3[15:0]), .row7(D3[31:16]), .row8(D4[15:0]), .row9(D4[31:16]), .row10(D5[15:0]),
    .row11(D5[31:16]), .row12(D6_2[15:0]), .row13(D6_2[31:16]), .row14(D7[15:0]), .row15(D7[31:16]));
  ROM #(.addrWidth(14), .dataWidth(32), .Select("high")) rom_7 (.addr(subtractor_2_out), .data(D3));
  ROM #(.addrWidth(14), .dataWidth(32), .Select("high")) rom_8 (.addr(subtractor_2_out), .data(D7));

  // Other names for the same wires on the sheet: D2[31:0] = D6; D6_t[31:0] = D6_2

  // Notes on the sheet:
  //   输入引脚区
  //   输入引脚区
  //   contents of rom_1 (hex, n*v repeats v):
  //   8*0 1000000 0 0 2400000 5*0 c0000 18000000 16*0 800000 0 0 0 10040000 7f00000 0 0 80000 800000 0 0 0
  //   c1803e0 0 600000 5*0 200000 0 18200000 180006 c003000 0 0 0 800000 1c00000 1c00000 200000 900000
  //   48003000 0 0 500000 0 40000 1c00000 38300000 800080 800080 3c00000 3c00000 c1803e0 1400080 1c00080 0
  //   0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
  //   contents of rom_2 (hex, n*v repeats v):
  //   0 0 0 180 0 4100410 c30 4400440 2600030 0 fe61c3 2400240 318c 4*0 400040 1000100 4000800 400020
  //   4800900 1200090 1000100 800080 2800280 500050 8800900 880048 7800700 f00070 800080 1400080 1ff8 0
  //   10040808 4100808 4000200 18181818 10041004 10041004 8000fc0 0 800040 800080 2400240 4000200 20022002
  //   40814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
  //   输出引脚区
  //   contents of rom_3 (hex, n*v repeats v):
  //   7*0 1100000 3000380 0 0 2400240 0 100008 c000c00 440022 33003300 600038 3000e00 400000 1000200
  //   2400000 2400000 10001f0 800080 20803f8 500070 8200ff0 20807f8 7e007f0 3f007f0 800080 0 0 0 2200140
  //   20020000 18041ffc 18183ffc 10041004 180c0c18 30000c0 18180000 100008 800080 1200120 100008 63001c0
  //   2002100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
  //   contents of rom_4 (hex, n*v repeats v):
  //   0 18002000 30000000 0 0 2200220 0 8800880 c001c0 0 38 2400240 5*0 400040 1000100 1000200 1000080
  //   2400480 2400120 1000100 800080 2800280 500050 8400880 1080088 7c00780 1f000f0 80 4100220 1800000
  //   1800000 20021004 2200410 8040400 18181818 10041004 10041004 4000800 18180000 3b001080 800080 4800480
  //   1ff80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
  //   汉字字库电路
  //   contents of rom_5 (hex, n*v repeats v):
  //   5*0 10041004 0 3300110 ffc0608 0 0 2400240 0 300030 10000800 cc00cc 44002200 400040 1000100 1000080
  //   400080 4800240 1200240 1000100 800080 28002f8 500050 8800840 880108 78007c0 f001f0 800080 4100808
  //   1800180 1800180 4100220 10042002 6000c04 18181818 10041004 10041004 4000400 1818 200010 800080
  //   1200120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
  //   contents of rom_6 (hex, n*v repeats v):
  //   0 c000c00 48004800 0 0 1c00140 0 11001100 4000e0 0 0 2400240 5*0 380060 e000300 400080 200 240 240
  //   1000100 f800080 3800280 10101fd0 ff00820 7f80208 7f007e0 7f003f0 ff8 808 180 180 2002 1400220
  //   1ffc1ffc 3c3c1818 c18180c 10041004 3000400 1818 c002e00 1ffc0080 4800480 0 0 c181004 c001200 c001200
  //   5*0 20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
  //   汉字显示验证区
  //   contents of rom_7 (hex, n*v repeats v):
  //   0 0 0 1800000 7f00000 8080808 c300000 6600330 10300c18 7ffe0000 3f800e00 2400240 318c0000 4*0 400040
  //   1000100 4000200 100020 9000480 900120 1000100 800080 2800280 500050 9000880 480088 7000780 7000f0
  //   800ff8 1400220 0 0 8080410 8081004 3000300 18181818 10041004 10041004 8000800 0 400020 800080
  //   2400240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
  //   contents of rom_8 (hex, n*v repeats v):
  //   0 0 3000 0 0 80 5*0 240 5*0 c 1800 7*0 1ff0 9*0 80 0 0 7f0 1004 c0 0 400 4*0 3e0 7*0 200 20c 0 60018
  //   30000c00 10*0 21c2 400 430 0 1c0 605e 2002 2002 0 0 3e0 80 80 7*0 80 80 3ffc 16*0 7b0 8*0 3ce6 1ef6
  //   9*0 9*808 11*1008 10*3e0 0 0 10*1008 23*0 4 2000 17*0 2000 c 0 3000 180 17*0 300048 9*0 7f8 2 ff0 9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
endmodule
