// Logisim project MIPS 寄存器文件验证实验.circ as structural Verilog: 7 circuits, main circuit MIPS寄存器文件电路
// MIPS寄存器文件
module \MIPS寄存器文件电路  (
  input  [4:0] R1_num,
  input  [4:0] R2_num,
  input  [31:0] Din,
  input  WE,
  input  CLK,
  input  [4:0] W_num,
  output [31:0] RD1,
  output [31:0] RD2
);

  wire and_1_out, and_2_out, and_3_out, and_4_out, and_5_out, and_6_out, and_7_out, and_8_out, and_9_out,
       and_10_out, and_11_out, and_12_out, and_13_out, and_14_out, and_15_out, and_16_out, and_17_out,
       and_18_out, and_19_out, and_20_out, and_21_out, and_22_out, and_23_out, and_24_out, and_25_out,
       and_26_out, and_27_out, and_28_out, and_29_out, and_30_out, and_31_out, and_32_out, and_33_out,
       and_34_out, and_35_out, and_36_out, decoder_1_out0, decoder_1_out1, decoder_1_out2, decoder_1_out3,
       decoder_2_out0, decoder_2_out1, decoder_2_out2, decoder_2_out3, decoder_2_out4, decoder_2_out5,
       decoder_2_out6, decoder_2_out7, decoder_3_out0, decoder_3_out1, decoder_3_out2, decoder_3_out3,
       decoder_3_out4, decoder_3_out5, decoder_3_out6, decoder_3_out7, decoder_4_out0, decoder_4_out1,
       decoder_4_out2, decoder_4_out3, decoder_4_out4, decoder_4_out5, decoder_4_out6, decoder_4_out7,
       decoder_5_out0, decoder_5_out1, decoder_5_out2, decoder_5_out3, decoder_5_out4, decoder_5_out5,
       decoder_5_out6, decoder_5_out7, RST;
  wire [31:0] register_1_q, register_2_q, register_3_q, register_4_q, register_5_q, register_6_q,
       register_7_q, register_8_q, register_9_q, register_10_q, register_11_q, register_12_q, register_13_q,
       register_14_q, register_15_q, register_16_q, register_17_q, register_18_q, register_19_q,
       register_20_q, register_21_q, register_22_q, register_23_q, register_24_q, register_25_q,
       register_26_q, register_27_q, register_28_q, register_29_q, register_30_q, register_31_q,
       register_32_q;

  Decoder #(.select(2), .tristate("false"), .disabled("Z"), .enable("false")) decoder_1 (
    .out0(decoder_1_out0), .out1(decoder_1_out1), .out2(decoder_1_out2), .out3(decoder_1_out3),
    .sel(W_num[4:3]));
  and and_1 (and_1_out, WE, decoder_1_out0);
  and and_2 (and_2_out, decoder_1_out1, WE);
  and and_3 (and_3_out, decoder_1_out2, WE);
  and and_4 (and_4_out, decoder_1_out3, WE);
  Decoder #(.select(3), .tristate("false"), .disabled("Z"), .enable("false")) decoder_2 (
    .out0(decoder_2_out0), .out1(decoder_2_out1), .out2(decoder_2_out2), .out3(decoder_2_out3),
    .out4(decoder_2_out4), .out5(decoder_2_out5), .out6(decoder_2_out6), .out7(decoder_2_out7),
    .sel(W_num[2:0]));
  Decoder #(.select(3), .tristate("false"), .disabled("Z"), .enable("false")) decoder_3 (
    .out0(decoder_3_out0), .out1(decoder_3_out1), .out2(decoder_3_out2), .out3(decoder_3_out3),
    .out4(decoder_3_out4), .out5(decoder_3_out5), .out6(decoder_3_out6), .out7(decoder_3_out7),
    .sel(W_num[2:0]));
  Decoder #(.select(3), .tristate("false"), .disabled("Z"), .enable("false")) decoder_4 (
    .out0(decoder_4_out0), .out1(decoder_4_out1), .out2(decoder_4_out2), .out3(decoder_4_out3),
    .out4(decoder_4_out4), .out5(decoder_4_out5), .out6(decoder_4_out6), .out7(decoder_4_out7),
    .sel(W_num[2:0]));
  Decoder #(.select(3), .tristate("false"), .disabled("Z"), .enable("false")) decoder_5 (
    .out0(decoder_5_out0), .out1(decoder_5_out1), .out2(decoder_5_out2), .out3(decoder_5_out3),
    .out4(decoder_5_out4), .out5(decoder_5_out5), .out6(decoder_5_out6), .out7(decoder_5_out7),
    .sel(W_num[2:0]));
  and and_5 (and_5_out, decoder_2_out0, and_1_out);
  and and_6 (and_6_out, decoder_2_out1, and_1_out);
  and and_7 (and_7_out, decoder_2_out2, and_1_out);
  and and_8 (and_8_out, decoder_2_out3, and_1_out);
  and and_9 (and_9_out, decoder_2_out4, and_1_out);
  and and_10 (and_10_out, decoder_2_out5, and_1_out);
  and and_11 (and_11_out, decoder_2_out6, and_1_out);
  and and_12 (and_12_out, decoder_2_out7, and_1_out);
  and and_13 (and_13_out, decoder_3_out0, and_2_out);
  and and_14 (and_14_out, decoder_3_out1, and_2_out);
  and and_15 (and_15_out, decoder_3_out2, and_2_out);
  and and_16 (and_16_out, decoder_3_out3, and_2_out);
  and and_17 (and_17_out, decoder_3_out4, and_2_out);
  and and_18 (and_18_out, decoder_3_out5, and_2_out);
  and and_19 (and_19_out, decoder_3_out6, and_2_out);
  and and_20 (and_20_out, decoder_3_out7, and_2_out);
  and and_21 (and_21_out, decoder_4_out0, and_3_out);
  and and_22 (and_22_out, decoder_4_out1, and_3_out);
  and and_23 (and_23_out, decoder_4_out2, and_3_out);
  and and_24 (and_24_out, decoder_4_out3, and_3_out);
  and and_25 (and_25_out, decoder_4_out4, and_3_out);
  and and_26 (and_26_out, decoder_4_out5, and_3_out);
  and and_27 (and_27_out, decoder_4_out6, and_3_out);
  and and_28 (and_28_out, decoder_4_out7, and_3_out);
  and and_29 (and_29_out, decoder_5_out0, and_4_out);
  and and_30 (and_30_out, decoder_5_out1, and_4_out);
  and and_31 (and_31_out, decoder_5_out2, and_4_out);
  and and_32 (and_32_out, decoder_5_out3, and_4_out);
  and and_33 (and_33_out, decoder_5_out4, and_4_out);
  and and_34 (and_34_out, decoder_5_out5, and_4_out);
  and and_35 (and_35_out, decoder_5_out6, and_4_out);
  and and_36 (and_36_out, decoder_5_out7, and_4_out);
  Register #(.width(32), .trigger("rising"), .Select("low")) register_1 (
    .D(Din), .en(and_5_out), .Q(register_1_q), .clk(CLK), .clr(RST));
  Register #(.width(32), .trigger("rising"), .Select("low")) register_2 (
    .D(Din), .en(and_6_out), .Q(register_2_q), .clk(CLK), .clr(RST));
  Register #(.width(32), .trigger("rising"), .Select("low")) register_3 (
    .D(Din), .en(and_7_out), .Q(register_3_q), .clk(CLK), .clr(RST));
  Register #(.width(32), .trigger("rising"), .Select("low")) register_4 (
    .D(Din), .en(and_8_out), .Q(register_4_q), .clk(CLK), .clr(RST));
  Register #(.width(32), .trigger("rising"), .Select("low")) register_5 (
    .D(Din), .en(and_9_out), .Q(register_5_q), .clk(CLK), .clr(RST));
  Register #(.width(32), .trigger("rising"), .Select("low")) register_6 (
    .D(Din), .en(and_10_out), .Q(register_6_q), .clk(CLK), .clr(RST));
  Register #(.width(32), .trigger("rising"), .Select("low")) register_7 (
    .D(Din), .en(and_11_out), .Q(register_7_q), .clk(CLK), .clr(RST));
  Register #(.width(32), .trigger("rising"), .Select("low")) register_8 (
    .D(Din), .en(and_12_out), .Q(register_8_q), .clk(CLK), .clr(RST));
  Register #(.width(32), .trigger("rising"), .Select("low")) register_9 (
    .D(Din), .en(and_13_out), .Q(register_9_q), .clk(CLK), .clr(RST));
  Register #(.width(32), .trigger("rising"), .Select("low")) register_10 (
    .D(Din), .en(and_14_out), .Q(register_10_q), .clk(CLK), .clr(RST));
  Register #(.width(32), .trigger("rising"), .Select("low")) register_11 (
    .D(Din), .en(and_15_out), .Q(register_11_q), .clk(CLK), .clr(RST));
  Register #(.width(32), .trigger("rising"), .Select("low")) register_12 (
    .D(Din), .en(and_16_out), .Q(register_12_q), .clk(CLK), .clr(RST));
  Register #(.width(32), .trigger("rising"), .Select("low")) register_13 (
    .D(Din), .en(and_17_out), .Q(register_13_q), .clk(CLK), .clr(RST));
  Register #(.width(32), .trigger("rising"), .Select("low")) register_14 (
    .D(Din), .en(and_18_out), .Q(register_14_q), .clk(CLK), .clr(RST));
  Register #(.width(32), .trigger("rising"), .Select("low")) register_15 (
    .D(Din), .en(and_19_out), .Q(register_15_q), .clk(CLK), .clr(RST));
  Register #(.width(32), .trigger("rising"), .Select("low")) register_16 (
    .D(Din), .en(and_20_out), .Q(register_16_q), .clk(CLK), .clr(RST));
  Register #(.width(32), .trigger("rising"), .Select("low")) register_17 (
    .D(Din), .en(and_21_out), .Q(register_17_q), .clk(CLK), .clr(RST));
  Register #(.width(32), .trigger("rising"), .Select("low")) register_18 (
    .D(Din), .en(and_22_out), .Q(register_18_q), .clk(CLK), .clr(RST));
  Register #(.width(32), .trigger("rising"), .Select("low")) register_19 (
    .D(Din), .en(and_23_out), .Q(register_19_q), .clk(CLK), .clr(RST));
  Register #(.width(32), .trigger("rising"), .Select("low")) register_20 (
    .D(Din), .en(and_24_out), .Q(register_20_q), .clk(CLK), .clr(RST));
  Register #(.width(32), .trigger("rising"), .Select("low")) register_21 (
    .D(Din), .en(and_25_out), .Q(register_21_q), .clk(CLK), .clr(RST));
  Register #(.width(32), .trigger("rising"), .Select("low")) register_22 (
    .D(Din), .en(and_26_out), .Q(register_22_q), .clk(CLK), .clr(RST));
  Register #(.width(32), .trigger("rising"), .Select("low")) register_23 (
    .D(Din), .en(and_27_out), .Q(register_23_q), .clk(CLK), .clr(RST));
  Register #(.width(32), .trigger("rising"), .Select("low")) register_24 (
    .D(Din), .en(and_28_out), .Q(register_24_q), .clk(CLK), .clr(RST));
  Register #(.width(32), .trigger("rising"), .Select("low")) register_25 (
    .D(Din), .en(and_29_out), .Q(register_25_q), .clk(CLK), .clr(RST));
  Register #(.width(32), .trigger("rising"), .Select("low")) register_26 (
    .D(Din), .en(and_30_out), .Q(register_26_q), .clk(CLK), .clr(RST));
  Register #(.width(32), .trigger("rising"), .Select("low")) register_27 (
    .D(Din), .en(and_31_out), .Q(register_27_q), .clk(CLK), .clr(RST));
  Register #(.width(32), .trigger("rising"), .Select("low")) register_28 (
    .D(Din), .en(and_32_out), .Q(register_28_q), .clk(CLK), .clr(RST));
  Register #(.width(32), .trigger("rising"), .Select("low")) register_29 (
    .D(Din), .en(and_33_out), .Q(register_29_q), .clk(CLK), .clr(RST));
  Register #(.width(32), .trigger("rising"), .Select("low")) register_30 (
    .D(Din), .en(and_34_out), .Q(register_30_q), .clk(CLK), .clr(RST));
  Register #(.width(32), .trigger("rising"), .Select("low")) register_31 (
    .D(Din), .en(and_35_out), .Q(register_31_q), .clk(CLK), .clr(RST));
  Register #(.width(32), .trigger("rising"), .Select("low")) register_32 (
    .D(Din), .en(and_36_out), .Q(register_32_q), .clk(CLK), .clr(RST));
  Button u_RST (.out(RST));
  Multiplexer #(.select(5), .width(32), .disabled("Z"), .enable("false")) multiplexer_1 (
    .in0(register_1_q), .in1(register_2_q), .in2(register_3_q), .in3(register_4_q), .in4(register_5_q),
    .in5(register_6_q), .in6(register_7_q), .in7(register_8_q), .in8(register_9_q), .in9(register_10_q),
    .in10(register_11_q), .in11(register_12_q), .in12(register_13_q), .in13(register_14_q),
    .in14(register_15_q), .in15(register_16_q), .in16(register_17_q), .in17(register_18_q),
    .in18(register_19_q), .in19(register_20_q), .in20(register_21_q), .in21(register_22_q),
    .in22(register_23_q), .in23(register_24_q), .in24(register_25_q), .in25(register_26_q),
    .in26(register_27_q), .in27(register_28_q), .in28(register_29_q), .in29(register_30_q),
    .in30(register_31_q), .in31(register_32_q), .out(RD1), .sel(R1_num));
  Multiplexer #(.select(5), .width(32), .disabled("Z"), .enable("false")) multiplexer_2 (
    .in0(register_1_q), .in1(register_2_q), .in2(register_3_q), .in3(register_4_q), .in4(register_5_q),
    .in5(register_6_q), .in6(register_7_q), .in7(register_8_q), .in8(register_9_q), .in9(register_10_q),
    .in10(register_11_q), .in11(register_12_q), .in12(register_13_q), .in13(register_14_q),
    .in14(register_15_q), .in15(register_16_q), .in16(register_17_q), .in17(register_18_q),
    .in18(register_19_q), .in19(register_20_q), .in20(register_21_q), .in21(register_22_q),
    .in22(register_23_q), .in23(register_24_q), .in24(register_25_q), .in25(register_26_q),
    .in26(register_27_q), .in27(register_28_q), .in28(register_29_q), .in29(register_30_q),
    .in30(register_31_q), .in31(register_32_q), .out(RD2), .sel(R2_num));

  // Notes on the sheet:
  //   输入引脚
  //   MIPS寄存器文件电路
  //   输出引脚
endmodule

module \简单的MIPS寄存器文件测试电路  (
  input  [4:0] R1_num,
  input  [4:0] R2_num,
  input  [4:0] W_num,
  input  WE,
  input  [31:0] Din,
  output [31:0] RD1,
  output [31:0] RD2
);

  wire CLK_out;

  // Probe on Din
  \MIPS寄存器文件电路  \mips寄存器文件电路_1  (
    .R1_num(R1_num), .R2_num(R2_num), .Din(Din), .W_num(W_num), .WE(WE), .CLK(CLK_out), .RD1(RD1), .RD2(RD2));
  Clock #(.highDuration(1), .lowDuration(1)) CLK (.out(CLK_out));
  // Probe on RD1
  // Probe on RD2

  // Notes on the sheet:
  //   R1#
  //   R2#
  //   W#
  //   WE
  //   Din
  //   RD1
  //   RD2
  //   CLK
  //   简单的MIPS寄存器文件测试电路
endmodule

module \复杂的MIPS寄存器文件测试电路  (
);

  wire and_1_out, CLK, comparator_1_eq, comparator_2_eq, comparator_3_eq, comparator_4_eq, Equal, Halt, NEQ,
       not_1_out, priority_encoder_1_gs, priority_encoder_2_gs, R1_NEQ, R2_NEQ, \评分逻辑电路_1_right ;
  wire [3:0] _1, _2, _3, and_2_out, and_3_out, and_4_out;
  wire [3:3] not_2_out;
  wire [9:0] counter_1_q, counter_2_q;
  wire [15:0] ErrorTrace, OtherInput;
  wire [31:0] R1_Ref, R2_Ref, Reg1, Reg2, WriteData, \评分逻辑电路_1_total , \评分逻辑电路_1_正确条数 ;

  Clock #(.highDuration(1), .lowDuration(1)) clock_1 (.out(CLK));
  Counter #(.width(10), .max('h3ff), .ongoal("wrap"), .trigger("rising"), .behavior("old")) counter_1 (
    .count(Halt), .Q(counter_1_q), .clk(CLK));  // open: load, D, carry, clr, preset
  LED #(.active("false")) \u_测试完成  (.in(Halt));
  Counter #(.width(10), .max('h3ff), .ongoal("wrap"), .trigger("rising"), .behavior("old")) counter_2 (
    .count(NEQ), .Q(counter_2_q), .clk(CLK), .clr(not_1_out));  // open: load, D, carry, preset
  not not_1 (not_1_out, Halt);
  ROM #(.addrWidth(10), .dataWidth(32), .Select("high")) \u_写入数据  (.addr(counter_1_q), .data(WriteData));
  ROM #(.addrWidth(10), .dataWidth(16), .Select("high")) \_3个寄存器编号和WE信号  (.addr(counter_1_q), .data(OtherInput));
  ROM #(.addrWidth(10), .dataWidth(32), .Select("high")) rom_1 (.addr(counter_1_q), .data(R1_Ref));
  and and_1 (and_1_out, Halt, NEQ);
  RAM #(.addrWidth(10), .dataWidth(16), .bus("separate"), .Select("high")) \u_错误记录  (
    .addr(counter_2_q), .din(ErrorTrace), .str(and_1_out), .clk(CLK));  // open: data, sel, ld, clr
  Hex_Digit_Display hex_digit_display_1 (.value(and_2_out));  // open: dp
  Hex_Digit_Display hex_digit_display_2 (.value(and_3_out));  // open: dp
  assign and_2_out = _2 & {4{not_2_out[3]}};  // AND_Gate and_2, 4 bits wide
  assign and_3_out = _3 & {4{not_2_out[3]}};  // AND_Gate and_3, 4 bits wide
  ROM #(.addrWidth(10), .dataWidth(32), .Select("high")) rom_2 (.addr(counter_1_q), .data(R2_Ref));
  Hex_Digit_Display hex_digit_display_3 (.value(and_4_out));  // open: dp
  assign and_4_out = _1 & {4{not_2_out[3]}};  // AND_Gate and_4, 4 bits wide
  \MIPS寄存器文件电路  \mips寄存器文件电路_1  (
    .R1_num(OtherInput[4:0]), .R2_num(OtherInput[9:5]), .Din(WriteData), .W_num(OtherInput[14:10]),
    .WE(OtherInput[15]), .CLK(CLK), .RD1(Reg1), .RD2(Reg2));
  not not_2 (not_2_out[3], Halt);
  Comparator #(.width(32), .mode("twosComplement")) comparator_1 (
    .a(R1_Ref), .b(Reg1), .eq(comparator_1_eq));  // open: gt, lt
  Comparator #(.width(32), .mode("twosComplement")) comparator_2 (
    .a(R2_Ref), .b(Reg2), .eq(comparator_2_eq));  // open: gt, lt
  // Probe on OtherInput[9:5]
  // Probe on OtherInput[4:0]
  Comparator #(.width(32), .mode("twosComplement")) comparator_3 (
    .a(WriteData), .b({32{1'b0}}), .eq(comparator_3_eq));  // open: gt, lt
  Comparator #(.width(16), .mode("twosComplement")) comparator_4 (
    .a(OtherInput), .b({16{1'b0}}), .eq(comparator_4_eq));  // open: gt, lt
  Priority_Encoder #(.select(1), .disabled("Z")) priority_encoder_1 (
    .in0(comparator_1_eq), .in1(comparator_1_eq), .gs(priority_encoder_1_gs));  // open: out, en_out, en_in
  Priority_Encoder #(.select(1), .disabled("Z")) priority_encoder_2 (
    .in0(comparator_2_eq), .in1(comparator_2_eq), .gs(priority_encoder_2_gs));  // open: out, en_out, en_in
  nand nand_1 (Halt, comparator_3_eq, comparator_4_eq);
  not not_3 (R1_NEQ, priority_encoder_1_gs);
  and and_5 (Equal, priority_encoder_1_gs, priority_encoder_2_gs);
  not not_4 (NEQ, Equal);
  not not_5 (R2_NEQ, priority_encoder_2_gs);
  Multiplexer #(.select(1), .width(8), .disabled("Z"), .enable("false")) multiplexer_1 (
    .in0({8{1'b1}}), .in1({3'b000, OtherInput[9:5]}), .out(ErrorTrace[7:0]), .sel(R2_NEQ));
  Multiplexer #(.select(1), .width(8), .disabled("Z"), .enable("false")) multiplexer_2 (
    .in0({8{1'b1}}), .in1({3'b000, OtherInput[4:0]}), .out(ErrorTrace[15:8]), .sel(R1_NEQ));
  // Probe on ErrorTrace
  LED #(.active("true")) \u_是否全部正确  (.in(\评分逻辑电路_1_right ));
  // Probe on \评分逻辑电路_1_total 
  // Probe on Reg1
  // Probe on R1_Ref
  // Probe on Reg2
  // Probe on R2_Ref
  \评分逻辑电路  \u_评分逻辑电路_1  (
    .CLK(CLK), .\正确条数 (\评分逻辑电路_1_正确条数 ), .High(_3), .Low(_1), .Mid(_2), .Right(\评分逻辑电路_1_right ),
    .Total(\评分逻辑电路_1_total ), .EQ(Equal), .EN(Halt));
  // Probe on \评分逻辑电路_1_正确条数 

  // Other names for the same wires on the sheet: R2_num[4:0] = OtherInput[9:5]; R1_num[4:0] = OtherInput[4:0];
  //   W_num[4:0] = OtherInput[14:10]

  // Notes on the sheet:
  //   期望值1
  //   contents of 写入数据 (hex, n*v repeats v):
  //   1 41b8 1bfe 2 44a8 1ca7 3 5f7a 2f2a 4 3d39 6009
  //   contents of _3个寄存器编号和WE信号 (hex, n*v repeats v):
  //   8041 c20 462 8441 820 62 8841 20 c62 8c41 820 462
  //   contents of rom_1 (hex, n*v repeats v):
  //   0 1 0 0 1 0 2 1 3 2 1 3 1
  //   R1#
  //   R2#
  //   期望值2
  //   成绩
  //   W#
  //   Din
  //   CLK
  //   WE
  //   contents of rom_2 (hex, n*v repeats v):
  //   4*0 2 0 0 2 0 3 2 4 1
  //   RD1
  //   RD2
  //   复杂的MIPS 寄存器文件测试电路
  //   容错处理
  //   停止信号
endmodule

// MIPS寄存器（R0=0）
module \MIPS_寄存器文件电路_R0_0  (
  input  [4:0] R1_num,
  input  [4:0] R2_num,
  input  [31:0] Din,
  input  WE,
  input  CLK,
  input  [4:0] W_num,
  output [31:0] RD1,
  output [31:0] RD2
);

  wire and_1_out, and_2_out, and_3_out, and_4_out, and_5_out, and_6_out, and_7_out, and_8_out, and_9_out,
       and_10_out, and_11_out, and_12_out, and_13_out, and_14_out, and_15_out, and_16_out, and_17_out,
       and_18_out, and_19_out, and_20_out, and_21_out, and_22_out, and_23_out, and_24_out, and_25_out,
       and_26_out, and_27_out, and_28_out, and_29_out, and_30_out, and_31_out, decoder_1_out1,
       decoder_1_out2, decoder_1_out3, decoder_1_out4, decoder_1_out5, decoder_1_out6, decoder_1_out7,
       decoder_1_out8, decoder_1_out9, decoder_1_out10, decoder_1_out11, decoder_1_out12, decoder_1_out13,
       decoder_1_out14, decoder_1_out15, decoder_1_out16, decoder_1_out17, decoder_1_out18, decoder_1_out19,
       decoder_1_out20, decoder_1_out21, decoder_1_out22, decoder_1_out23, decoder_1_out24, decoder_1_out25,
       decoder_1_out26, decoder_1_out27, decoder_1_out28, decoder_1_out29, decoder_1_out30, decoder_1_out31;
  wire [31:0] register_1_q, register_2_q, register_3_q, register_4_q, register_5_q, register_6_q,
       register_7_q, register_8_q, register_9_q, register_10_q, register_11_q, register_12_q, register_13_q,
       register_14_q, register_15_q, register_16_q, register_17_q, register_18_q, register_19_q,
       register_20_q, register_21_q, register_22_q, register_23_q, register_24_q, register_25_q,
       register_26_q, register_27_q, register_28_q, register_29_q, register_30_q, register_31_q,
       register_32_q;

  Decoder #(.select(5), .tristate("false"), .disabled("Z"), .enable("false")) decoder_1 (
    .out1(decoder_1_out1), .out2(decoder_1_out2), .out3(decoder_1_out3), .out4(decoder_1_out4),
    .out5(decoder_1_out5), .out6(decoder_1_out6), .out7(decoder_1_out7), .out8(decoder_1_out8),
    .out9(decoder_1_out9), .out10(decoder_1_out10), .out11(decoder_1_out11), .out12(decoder_1_out12),
    .out13(decoder_1_out13), .out14(decoder_1_out14), .out15(decoder_1_out15), .out16(decoder_1_out16),
    .out17(decoder_1_out17), .out18(decoder_1_out18), .out19(decoder_1_out19), .out20(decoder_1_out20),
    .out21(decoder_1_out21), .out22(decoder_1_out22), .out23(decoder_1_out23), .out24(decoder_1_out24),
    .out25(decoder_1_out25), .out26(decoder_1_out26), .out27(decoder_1_out27), .out28(decoder_1_out28),
    .out29(decoder_1_out29), .out30(decoder_1_out30), .out31(decoder_1_out31), .sel(W_num));  // open: out0
  and and_1 (and_1_out, decoder_1_out1, WE);
  and and_2 (and_2_out, decoder_1_out2, WE);
  and and_3 (and_3_out, decoder_1_out3, WE);
  and and_4 (and_4_out, decoder_1_out4, WE);
  and and_5 (and_5_out, decoder_1_out5, WE);
  and and_6 (and_6_out, decoder_1_out6, WE);
  and and_7 (and_7_out, decoder_1_out7, WE);
  and and_8 (and_8_out, decoder_1_out8, WE);
  and and_9 (and_9_out, decoder_1_out9, WE);
  and and_10 (and_10_out, decoder_1_out10, WE);
  and and_11 (and_11_out, decoder_1_out11, WE);
  and and_12 (and_12_out, decoder_1_out12, WE);
  and and_13 (and_13_out, decoder_1_out13, WE);
  and and_14 (and_14_out, decoder_1_out14, WE);
  and and_15 (and_15_out, decoder_1_out15, WE);
  and and_16 (and_16_out, decoder_1_out16, WE);
  and and_17 (and_17_out, decoder_1_out17, WE);
  and and_18 (and_18_out, decoder_1_out18, WE);
  and and_19 (and_19_out, decoder_1_out19, WE);
  and and_20 (and_20_out, decoder_1_out20, WE);
  and and_21 (and_21_out, decoder_1_out21, WE);
  and and_22 (and_22_out, decoder_1_out22, WE);
  and and_23 (and_23_out, decoder_1_out23, WE);
  and and_24 (and_24_out, decoder_1_out24, WE);
  and and_25 (and_25_out, decoder_1_out25, WE);
  and and_26 (and_26_out, decoder_1_out26, WE);
  and and_27 (and_27_out, decoder_1_out27, WE);
  and and_28 (and_28_out, decoder_1_out28, WE);
  and and_29 (and_29_out, decoder_1_out29, WE);
  and and_30 (and_30_out, decoder_1_out30, WE);
  and and_31 (and_31_out, decoder_1_out31, WE);
  Register #(.width(32), .trigger("rising"), .Select("low")) register_1 (
    .D({32{1'b0}}), .en(WE), .Q(register_1_q), .clk(CLK));  // open: clr
  Register #(.width(32), .trigger("rising"), .Select("low")) register_2 (
    .D(Din), .en(and_1_out), .Q(register_2_q), .clk(CLK));  // open: clr
  Register #(.width(32), .trigger("rising"), .Select("low")) register_3 (
    .D(Din), .en(and_2_out), .Q(register_3_q), .clk(CLK));  // open: clr
  Register #(.width(32), .trigger("rising"), .Select("low")) register_4 (
    .D(Din), .en(and_3_out), .Q(register_4_q), .clk(CLK));  // open: clr
  Register #(.width(32), .trigger("rising"), .Select("low")) register_5 (
    .D(Din), .en(and_4_out), .Q(register_5_q), .clk(CLK));  // open: clr
  Register #(.width(32), .trigger("rising"), .Select("low")) register_6 (
    .D(Din), .en(and_5_out), .Q(register_6_q), .clk(CLK));  // open: clr
  Register #(.width(32), .trigger("rising"), .Select("low")) register_7 (
    .D(Din), .en(and_6_out), .Q(register_7_q), .clk(CLK));  // open: clr
  Register #(.width(32), .trigger("rising"), .Select("low")) register_8 (
    .D(Din), .en(and_7_out), .Q(register_8_q), .clk(CLK));  // open: clr
  Register #(.width(32), .trigger("rising"), .Select("low")) register_9 (
    .D(Din), .en(and_8_out), .Q(register_9_q), .clk(CLK));  // open: clr
  Register #(.width(32), .trigger("rising"), .Select("low")) register_10 (
    .D(Din), .en(and_9_out), .Q(register_10_q), .clk(CLK));  // open: clr
  Register #(.width(32), .trigger("rising"), .Select("low")) register_11 (
    .D(Din), .en(and_10_out), .Q(register_11_q), .clk(CLK));  // open: clr
  Register #(.width(32), .trigger("rising"), .Select("low")) register_12 (
    .D(Din), .en(and_11_out), .Q(register_12_q), .clk(CLK));  // open: clr
  Register #(.width(32), .trigger("rising"), .Select("low")) register_13 (
    .D(Din), .en(and_12_out), .Q(register_13_q), .clk(CLK));  // open: clr
  Register #(.width(32), .trigger("rising"), .Select("low")) register_14 (
    .D(Din), .en(and_13_out), .Q(register_14_q), .clk(CLK));  // open: clr
  Register #(.width(32), .trigger("rising"), .Select("low")) register_15 (
    .D(Din), .en(and_14_out), .Q(register_15_q), .clk(CLK));  // open: clr
  Register #(.width(32), .trigger("rising"), .Select("low")) register_16 (
    .D(Din), .en(and_15_out), .Q(register_16_q), .clk(CLK));  // open: clr
  Register #(.width(32), .trigger("rising"), .Select("low")) register_17 (
    .D(Din), .en(and_16_out), .Q(register_17_q), .clk(CLK));  // open: clr
  Register #(.width(32), .trigger("rising"), .Select("low")) register_18 (
    .D(Din), .en(and_17_out), .Q(register_18_q), .clk(CLK));  // open: clr
  Register #(.width(32), .trigger("rising"), .Select("low")) register_19 (
    .D(Din), .en(and_18_out), .Q(register_19_q), .clk(CLK));  // open: clr
  Register #(.width(32), .trigger("rising"), .Select("low")) register_20 (
    .D(Din), .en(and_19_out), .Q(register_20_q), .clk(CLK));  // open: clr
  Register #(.width(32), .trigger("rising"), .Select("low")) register_21 (
    .D(Din), .en(and_20_out), .Q(register_21_q), .clk(CLK));  // open: clr
  Register #(.width(32), .trigger("rising"), .Select("low")) register_22 (
    .D(Din), .en(and_21_out), .Q(register_22_q), .clk(CLK));  // open: clr
  Register #(.width(32), .trigger("rising"), .Select("low")) register_23 (
    .D(Din), .en(and_22_out), .Q(register_23_q), .clk(CLK));  // open: clr
  Register #(.width(32), .trigger("rising"), .Select("low")) register_24 (
    .D(Din), .en(and_23_out), .Q(register_24_q), .clk(CLK));  // open: clr
  Register #(.width(32), .trigger("rising"), .Select("low")) register_25 (
    .D(Din), .en(and_24_out), .Q(register_25_q), .clk(CLK));  // open: clr
  Register #(.width(32), .trigger("rising"), .Select("low")) register_26 (
    .D(Din), .en(and_25_out), .Q(register_26_q), .clk(CLK));  // open: clr
  Register #(.width(32), .trigger("rising"), .Select("low")) register_27 (
    .D(Din), .en(and_26_out), .Q(register_27_q), .clk(CLK));  // open: clr
  Register #(.width(32), .trigger("rising"), .Select("low")) register_28 (
    .D(Din), .en(and_27_out), .Q(register_28_q), .clk(CLK));  // open: clr
  Register #(.width(32), .trigger("rising"), .Select("low")) register_29 (
    .D(Din), .en(and_28_out), .Q(register_29_q), .clk(CLK));  // open: clr
  Register #(.width(32), .trigger("rising"), .Select("low")) register_30 (
    .D(Din), .en(and_29_out), .Q(register_30_q), .clk(CLK));  // open: clr
  Register #(.width(32), .trigger("rising"), .Select("low")) register_31 (
    .D(Din), .en(and_30_out), .Q(register_31_q), .clk(CLK));  // open: clr
  Register #(.width(32), .trigger("rising"), .Select("low")) register_32 (
    .D(Din), .en(and_31_out), .Q(register_32_q), .clk(CLK));  // open: clr
  Multiplexer #(.select(5), .width(32), .disabled("Z"), .enable("false")) multiplexer_1 (
    .in0(register_1_q), .in1(register_2_q), .in2(register_3_q), .in3(register_4_q), .in4(register_5_q),
    .in5(register_6_q), .in6(register_7_q), .in7(register_8_q), .in8(register_9_q), .in9(register_10_q),
    .in10(register_11_q), .in11(register_12_q), .in12(register_13_q), .in13(register_14_q),
    .in14(register_15_q), .in15(register_16_q), .in16(register_17_q), .in17(register_18_q),
    .in18(register_19_q), .in19(register_20_q), .in20(register_21_q), .in21(register_22_q),
    .in22(register_23_q), .in23(register_24_q), .in24(register_25_q), .in25(register_26_q),
    .in26(register_27_q), .in27(register_28_q), .in28(register_29_q), .in29(register_30_q),
    .in30(register_31_q), .in31(register_32_q), .out(RD1), .sel(R1_num));
  Multiplexer #(.select(5), .width(32), .disabled("Z"), .enable("false")) multiplexer_2 (
    .in0(register_1_q), .in1(register_2_q), .in2(register_3_q), .in3(register_4_q), .in4(register_5_q),
    .in5(register_6_q), .in6(register_7_q), .in7(register_8_q), .in8(register_9_q), .in9(register_10_q),
    .in10(register_11_q), .in11(register_12_q), .in12(register_13_q), .in13(register_14_q),
    .in14(register_15_q), .in15(register_16_q), .in16(register_17_q), .in17(register_18_q),
    .in18(register_19_q), .in19(register_20_q), .in20(register_21_q), .in21(register_22_q),
    .in22(register_23_q), .in23(register_24_q), .in24(register_25_q), .in25(register_26_q),
    .in26(register_27_q), .in27(register_28_q), .in28(register_29_q), .in29(register_30_q),
    .in30(register_31_q), .in31(register_32_q), .out(RD2), .sel(R2_num));

  // Notes on the sheet:
  //   输入引脚
  //   MIPS 寄存器文件电路（R0=0）
  //   输出引脚
endmodule

module \简单的MIPS寄存器文件测试电路_R0_0  (
  input  [4:0] R1_num,
  input  [4:0] R2_num,
  input  [4:0] W_num,
  input  WE,
  input  [31:0] Din,
  output [31:0] RD1,
  output [31:0] RD2
);

  wire CLK_out;

  // Probe on Din
  \MIPS_寄存器文件电路_R0_0  \mips_寄存器文件电路_r0_0_1  (
    .R1_num(R1_num), .R2_num(R2_num), .Din(Din), .W_num(W_num), .WE(WE), .CLK(CLK_out), .RD1(RD1), .RD2(RD2));
  Clock #(.highDuration(1), .lowDuration(1)) CLK (.out(CLK_out));
  // Probe on RD1
  // Probe on RD2

  // Notes on the sheet:
  //   R1#
  //   R2#
  //   W#
  //   Din
  //   WE
  //   RD1
  //   RD2
  //   CLK
  //   简单的MIPS 寄存器文件测试电路（R0=0）
endmodule

module \复杂的MIPS寄存器文件测试电路_R0_0  (
);

  wire and_1_out, CLK, comparator_1_eq, comparator_2_eq, comparator_3_eq, comparator_4_eq, Equal, Halt, NEQ,
       not_1_out, priority_encoder_1_gs, priority_encoder_2_gs, R1_NEQ, R2_NEQ, \评分逻辑电路_1_right ;
  wire [3:0] _1, _2, _3, and_2_out, and_3_out, and_4_out;
  wire [3:3] not_2_out;
  wire [9:0] counter_1_q, counter_2_q;
  wire [15:0] ErrorTrace, OtherInput;
  wire [31:0] R1_Ref, R2_Ref, Reg1, Reg2, WriteData, \评分逻辑电路_1_total , \评分逻辑电路_1_正确条数 ;

  Clock #(.highDuration(1), .lowDuration(1)) clock_1 (.out(CLK));
  Counter #(.width(10), .max('h3ff), .ongoal("wrap"), .trigger("rising"), .behavior("old")) counter_1 (
    .count(Halt), .Q(counter_1_q), .clk(CLK));  // open: load, D, carry, clr, preset
  LED #(.active("false")) \u_测试完成  (.in(Halt));
  Counter #(.width(10), .max('h3ff), .ongoal("wrap"), .trigger("rising"), .behavior("old")) counter_2 (
    .count(NEQ), .Q(counter_2_q), .clk(CLK), .clr(not_1_out));  // open: load, D, carry, preset
  not not_1 (not_1_out, Halt);
  ROM #(.addrWidth(10), .dataWidth(32), .Select("high")) \u_写入数据  (.addr(counter_1_q), .data(WriteData));
  ROM #(.addrWidth(10), .dataWidth(16), .Select("high")) \_3个寄存器编号和WE信号  (.addr(counter_1_q), .data(OtherInput));
  ROM #(.addrWidth(10), .dataWidth(32), .Select("high")) rom_1 (.addr(counter_1_q), .data(R1_Ref));
  and and_1 (and_1_out, Halt, NEQ);
  RAM #(.addrWidth(10), .dataWidth(16), .bus("separate"), .Select("high")) \u_错误记录  (
    .addr(counter_2_q), .din(ErrorTrace), .str(and_1_out), .clk(CLK));  // open: data, sel, ld, clr
  Hex_Digit_Display hex_digit_display_1 (.value(and_3_out));  // open: dp
  Hex_Digit_Display hex_digit_display_2 (.value(and_2_out));  // open: dp
  assign and_2_out = _2 & {4{not_2_out[3]}};  // AND_Gate and_2, 4 bits wide
  assign and_3_out = _3 & {4{not_2_out[3]}};  // AND_Gate and_3, 4 bits wide
  ROM #(.addrWidth(10), .dataWidth(32), .Select("high")) rom_2 (.addr(counter_1_q), .data(R2_Ref));
  Hex_Digit_Display hex_digit_display_3 (.value(and_4_out));  // open: dp
  assign and_4_out = _1 & {4{not_2_out[3]}};  // AND_Gate and_4, 4 bits wide
  \MIPS_寄存器文件电路_R0_0  \mips_寄存器文件电路_r0_0_1  (
    .R1_num(OtherInput[4:0]), .R2_num(OtherInput[9:5]), .Din(WriteData), .W_num(OtherInput[14:10]),
    .WE(OtherInput[15]), .CLK(CLK), .RD1(Reg1), .RD2(Reg2));
  not not_2 (not_2_out[3], Halt);
  Comparator #(.width(32), .mode("twosComplement")) comparator_1 (
    .a(R1_Ref), .b(Reg1), .eq(comparator_1_eq));  // open: gt, lt
  Comparator #(.width(32), .mode("twosComplement")) comparator_2 (
    .a(R2_Ref), .b(Reg2), .eq(comparator_2_eq));  // open: gt, lt
  // Probe on OtherInput[9:5]
  // Probe on OtherInput[4:0]
  Comparator #(.width(32), .mode("twosComplement")) comparator_3 (
    .a(WriteData), .b({32{1'b0}}), .eq(comparator_3_eq));  // open: gt, lt
  Comparator #(.width(16), .mode("twosComplement")) comparator_4 (
    .a(OtherInput), .b({16{1'b0}}), .eq(comparator_4_eq));  // open: gt, lt
  Priority_Encoder #(.select(1), .disabled("Z")) priority_encoder_1 (
    .in0(comparator_1_eq), .in1(comparator_1_eq), .gs(priority_encoder_1_gs));  // open: out, en_out, en_in
  Priority_Encoder #(.select(1), .disabled("Z")) priority_encoder_2 (
    .in0(comparator_2_eq), .in1(comparator_2_eq), .gs(priority_encoder_2_gs));  // open: out, en_out, en_in
  nand nand_1 (Halt, comparator_3_eq, comparator_4_eq);
  not not_3 (R1_NEQ, priority_encoder_1_gs);
  and and_5 (Equal, priority_encoder_1_gs, priority_encoder_2_gs);
  not not_4 (NEQ, Equal);
  not not_5 (R2_NEQ, priority_encoder_2_gs);
  Multiplexer #(.select(1), .width(8), .disabled("Z"), .enable("false")) multiplexer_1 (
    .in0({8{1'b1}}), .in1({3'b000, OtherInput[9:5]}), .out(ErrorTrace[7:0]), .sel(R2_NEQ));
  Multiplexer #(.select(1), .width(8), .disabled("Z"), .enable("false")) multiplexer_2 (
    .in0({8{1'b1}}), .in1({3'b000, OtherInput[4:0]}), .out(ErrorTrace[15:8]), .sel(R1_NEQ));
  // Probe on ErrorTrace
  LED #(.active("true")) \u_是否全部正确  (.in(\评分逻辑电路_1_right ));
  // Probe on \评分逻辑电路_1_total 
  // Probe on Reg1
  // Probe on R1_Ref
  // Probe on Reg2
  // Probe on R2_Ref
  \评分逻辑电路  \u_评分逻辑电路_1  (
    .CLK(CLK), .\正确条数 (\评分逻辑电路_1_正确条数 ), .High(_3), .Low(_1), .Mid(_2), .Right(\评分逻辑电路_1_right ),
    .Total(\评分逻辑电路_1_total ), .EQ(Equal), .EN(Halt));
  // Probe on \评分逻辑电路_1_正确条数 

  // Other names for the same wires on the sheet: R2_num[4:0] = OtherInput[9:5]; R1_num[4:0] = OtherInput[4:0];
  //   W_num[4:0] = OtherInput[14:10]

  // Notes on the sheet:
  //   期望值1
  //   contents of 写入数据 (hex, n*v repeats v):
  //   1 41b8 1bfe 2 44a8 1ca7 3 5f7a 2f2a 4 3d39 6009
  //   contents of _3个寄存器编号和WE信号 (hex, n*v repeats v):
  //   8041 c20 462 8441 820 62 8841 20 c62 8c41 820 462
  //   contents of rom_1 (hex, n*v repeats v):
  //   6*0 2 0 3 2 0 3 1
  //   R1#
  //   R2#
  //   W#
  //   期望值2
  //   成绩
  //   Din
  //   WE
  //   CLK
  //   contents of rom_2 (hex, n*v repeats v):
  //   4*0 2 0 0 2 0 3 2 4 1
  //   RD1
  //   RD2
  //   复杂的MIPS 寄存器文件测试电路（R0=0）
  //   容错处理
  //   停止信号
endmodule

// 评分逻辑
module \评分逻辑电路  (
  input  EQ,
  input  EN,
  input  CLK,
  output [31:0] \正确条数 ,
  output [3:0] High,
  output [3:0] Low,
  output [3:0] Mid,
  output [31:0] Total,
  output Right
);

  wire and_1_out, priority_encoder_1_gs, priority_encoder_1_out;
  wire [31:0] divider_1_out, divider_2_out, multiplier_1_out;
  wire [31:4] divider_2_rem, divider_3_out, divider_3_rem;

  Counter #(.width(32), .max('hffffffff), .ongoal("wrap"), .trigger("rising"), .behavior("old")) counter_1 (
    .count(EN), .Q(Total), .clk(CLK));  // open: load, D, carry, clr, preset
  Priority_Encoder #(.select(1), .disabled("Z")) priority_encoder_1 (
    .in0(EQ), .in1(EQ), .out(priority_encoder_1_out), .gs(priority_encoder_1_gs));  // open: en_out, en_in
  and and_1 (and_1_out, priority_encoder_1_out, priority_encoder_1_gs, EN);
  Counter #(.width(32), .max('hffffffff), .ongoal("wrap"), .trigger("rising"), .behavior("old")) counter_2 (
    .count(and_1_out), .Q(\正确条数 ), .clk(CLK));  // open: load, D, carry, clr, preset
  Multiplier #(.width(32)) multiplier_1 (.a(\正确条数 ), .b(32'h64), .out(multiplier_1_out));  // open: cin, cout
  Divider #(.width(32)) divider_1 (.a(multiplier_1_out), .b(Total), .out(divider_1_out));  // open: upper, rem
  Comparator #(.width(32), .mode("twosComplement")) comparator_1 (.a(\正确条数 ), .b(Total), .eq(Right));  // open: gt, lt
  Divider #(.width(32)) divider_2 (
    .a(divider_1_out), .b(32'ha), .out(divider_2_out), .rem({divider_2_rem, Low}));  // open: upper
  Divider #(.width(32)) divider_3 (
    .a(divider_2_out), .b(32'ha), .out({divider_3_out, High}), .rem({divider_3_rem, Mid}));  // open: upper

  // Notes on the sheet:
  //   评分逻辑电路
endmodule
