// Logisim project cache 设计实验.circ as structural Verilog: 8 circuits, main circuit cache（直接相联映射）电路（4个cache块）
// 直接相联cache
module \cache_直接相联映射_电路_4个cache块  (
  input  [15:0] Addr,
  input  [31:0] BlockDataIn,
  input  BlkDataReady,
  input  CLK,
  output Miss,
  output [7:0] DataOut
);


  // Other names for the same wires on the sheet: Blk[31:0] = BlockDataIn; BlkReady = BlkDataReady; 字节地址[15:0] = Addr

  // Notes on the sheet:
  //   输入引脚区
  //   cache（直接相联映射）电路（4个cache块）
  //   请同学们在此设计电路！
  //   输出引脚区
endmodule

// 直接相联cache
module \cache_直接相联映射_电路_16个cache块  (
  input  [15:0] Addr,
  input  [31:0] BlockDataIn,
  input  BlkDataReady,
  input  CLK,
  output Miss,
  output [7:0] DataOut
);


  // Other names for the same wires on the sheet: Blk[31:0] = BlockDataIn; BlkReady = BlkDataReady; 字节地址[15:0] = Addr

  // Notes on the sheet:
  //   输入引脚区
  //   cache（直接相联映射）电路（16个cache块）
  //   请同学们在此设计电路！
  //   输出引脚区
endmodule

// 全相联cache
module \cache_全相联映射_电路_4个cache块  (
  input  BlkDataReady,
  input  [15:0] Addr,
  input  [31:0] BlockDataIn,
  input  CLK,
  output Miss,
  output [7:0] DataOut
);


  // Other names for the same wires on the sheet: Blk[31:0] = BlockDataIn; BlkReady = BlkDataReady; 字节地址[15:0] = Addr

  // Notes on the sheet:
  //   输入引脚区
  //   cache（全相联映射）电路（4个cache块）
  //   请同学们在此设计电路！
  //   输出引脚区
endmodule

// 全相联cache
module \cache_全相联映射_电路_16个cache块  (
  input  BlkDataReady,
  input  [15:0] Addr,
  input  [31:0] BlockDataIn,
  input  CLK,
  output Miss,
  output [7:0] DataOut
);


  // Other names for the same wires on the sheet: Blk[31:0] = BlockDataIn; BlkReady = BlkDataReady; 字节地址[15:0] = Addr

  // Notes on the sheet:
  //   输入引脚区
  //   cache（全相联映射）电路（16个cache块）
  //   请同学们在此设计电路！
  //   输出引脚区
endmodule

// 2路组相联cache
module \cache_2路组相联映射_电路_4个cache块  (
  input  BlkDataReady,
  input  [15:0] Addr,
  input  [31:0] BlockDataIn,
  input  CLK,
  output Miss,
  output [7:0] DataOut
);


  // Other names for the same wires on the sheet: Blk[31:0] = BlockDataIn; BlkReady = BlkDataReady; 字节地址[15:0] = Addr

  // Notes on the sheet:
  //   输入引脚区
  //   cache（2路组相联映射）电路（4个cache块）
  //   请同学们在此设计电路！
  //   输出引脚区
endmodule

// 2路组相联cache
module \cache_2路组相联_电路_16个cache块  (
  input  BlkDataReady,
  input  [15:0] Addr,
  input  [31:0] BlockDataIn,
  input  CLK,
  output Miss,
  output [7:0] DataOut
);


  // Other names for the same wires on the sheet: Blk[31:0] = BlockDataIn; BlkReady = BlkDataReady; 字节地址[15:0] = Addr

  // Notes on the sheet:
  //   输入引脚区
  //   cache（2路组相联映射）电路（16个cache块）
  //   请同学们在此设计电路！
  //   输出引脚区
endmodule

// 4路组相联cache
module \cache_4路组相联映射_电路_16个cache块  (
  input  BlkDataReady,
  input  [31:0] BlockDataIn,
  input  [15:0] Addr,
  input  CLK,
  output Miss,
  output [7:0] DataOut
);


  // Other names for the same wires on the sheet: Blk[31:0] = BlockDataIn; BlkReady = BlkDataReady; 字节地址[15:0] = Addr

  // Notes on the sheet:
  //   输入引脚区
  //   cache（4路组相联映射）电路（16个cache块）
  //   请同学们在此设计电路！
  //   输出引脚区
endmodule

// 8路组相联cache
module \cache_8路组相联映射_电路_16个cache块  (
  input  BlkDataReady,
  input  [31:0] BlockDataIn,
  input  [15:0] Addr,
  input  CLK,
  output Miss,
  output [7:0] DataOut
);


  // Other names for the same wires on the sheet: Blk[31:0] = BlockDataIn; BlkReady = BlkDataReady; 字节地址[15:0] = Addr

  // Notes on the sheet:
  //   输入引脚区
  //   cache（8路组相联映射）电路（16个cache块）
  //   请同学们在此设计电路！
  //   输出引脚区
endmodule
