// Logisim project 存储器组件验证实验.circ as structural Verilog: 4 circuits, main circuit ROM存储器组件电路
module \ROM存储器组件电路  (
  input  CLR,
  input  SEL,
  output [31:0] out_3
);

  wire CLK_out;
  wire [7:0] counter_1_q;

  Clock #(.highDuration(1), .lowDuration(1)) CLK (.out(CLK_out));
  Counter #(.width(8), .max('hff), .ongoal("wrap"), .trigger("rising"), .behavior("new")) counter_1 (
    .load(1'b0), .D({8{1'b0}}), .count(1'b1), .Q(counter_1_q), .clk(CLK_out), .clr(CLR), .preset(1'b0),
    .down(1'b0));  // open: carry
  // Probe on counter_1_q
  ROM #(.addrWidth(8), .dataWidth(32), .Select("low")) rom_1 (.addr(counter_1_q), .data(out_3), .sel(SEL));
  // Probe on out_3

  // Notes on the sheet:
  //   计数器
  //   ROM
  //   contents of rom_1 (hex, n*v repeats v):
  //   11111111 22222222 33333333 44444444 55555555 66666666 77777777 88888888 99999999 aaaaaaaa bbbbbbbb
  //   cccccccc dddddddd eeeeeeee ffffffff
  //   ROM存储器组件电路
endmodule

module \RAM存储器组件电路_同步模式  (
  input  CLR,
  input  SEL,
  input  LD,
  input  CLR_2,
  output [31:0] out_5
);

  wire CLK_out;
  wire [7:0] counter_1_q;

  Clock #(.highDuration(1), .lowDuration(1)) CLK (.out(CLK_out));
  Counter #(.width(8), .max('hff), .ongoal("wrap"), .trigger("rising"), .behavior("new")) counter_1 (
    .load(1'b0), .D({8{1'b0}}), .count(1'b1), .Q(counter_1_q), .clk(CLK_out), .clr(CLR), .preset(1'b0),
    .down(1'b0));  // open: carry
  // Probe on counter_1_q
  RAM #(.addrWidth(8), .dataWidth(32), .bus("combined"), .Select("low")) ram_1 (
    .addr(counter_1_q), .data(out_5), .sel(SEL), .clk(CLK_out), .ld(LD), .clr(CLR_2));
  // Probe on out_5

  // Notes on the sheet:
  //   计数器
  //   RAM-1
  //   RAM存储器组件电路（同步模式）
endmodule

module \RAM存储器组件电路_异步模式  (
  input  CLR,
  input  SEL,
  input  LD,
  input  CLR_2,
  output [31:0] out_5
);

  wire CLK_out;
  wire [7:0] counter_1_q;

  Clock #(.highDuration(1), .lowDuration(1)) CLK (.out(CLK_out));
  Counter #(.width(8), .max('hff), .ongoal("wrap"), .trigger("rising"), .behavior("new")) counter_1 (
    .load(1'b0), .D({8{1'b0}}), .count(1'b1), .Q(counter_1_q), .clk(CLK_out), .clr(CLR), .preset(1'b0),
    .down(1'b0));  // open: carry
  // Probe on counter_1_q
  RAM #(.addrWidth(8), .dataWidth(32), .bus("asynch"), .Select("low")) ram_1 (
    .addr(counter_1_q), .data(out_5), .sel(SEL), .ld(LD), .clr(CLR_2));
  // Probe on out_5

  // Notes on the sheet:
  //   计数器
  //   RAM-2
  //   RAM存储器组件电路（异步模式）
endmodule

module \RAM存储器组件电路_分离模式  (
  input  CLR,
  input  STR,
  input  SEL,
  input  LD,
  input  CLR_2,
  input  [31:0] in_6,
  output [31:0] out_7
);

  wire CLK_out;
  wire [7:0] counter_1_q;

  Clock #(.highDuration(1), .lowDuration(1)) CLK (.out(CLK_out));
  Counter #(.width(8), .max('hff), .ongoal("wrap"), .trigger("rising"), .behavior("new")) counter_1 (
    .load(1'b0), .D({8{1'b0}}), .count(1'b1), .Q(counter_1_q), .clk(CLK_out), .clr(CLR), .preset(1'b0),
    .down(1'b0));  // open: carry
  // Probe on in_6
  // Probe on counter_1_q
  RAM #(.addrWidth(8), .dataWidth(32), .bus("separate"), .Select("low")) ram_1 (
    .addr(counter_1_q), .din(in_6), .data(out_7), .str(STR), .sel(SEL), .clk(CLK_out), .ld(LD), .clr(CLR_2));
  // Probe on out_7

  // Notes on the sheet:
  //   Din
  //   计数器
  //   Din
  //   RAM-3
  //   RAM存储器组件电路（分离模式）
  //   Dout
  //   Dout
endmodule
