// Logisim project 6位补码阵列乘法器.circ as structural Verilog: 3 circuits, main circuit 6位补码阵列乘法器
module \_6位补码阵列乘法器  (
  input  [5:0] X,
  input  [5:0] Y,
  output [11:0] P
);

  wire \n1位全加器fa_2_cout , \n1位全加器fa_3_cout , \n1位全加器fa_3_si , \n1位全加器fa_4_cout , \n1位全加器fa_5_cout ,
       \n1位全加器fa_5_si , \n1位全加器fa_6_cout , \n1位全加器fa_6_si , \n1位全加器fa_7_cout , \n1位全加器fa_8_cout ,
       \n1位全加器fa_8_si , \n1位全加器fa_9_cout , \n1位全加器fa_9_si , \n1位全加器fa_10_cout , \n1位全加器fa_10_si ,
       \n1位全加器fa_11_cout , \n1位全加器fa_12_cout , \n1位全加器fa_12_si , \n1位全加器fa_13_cout , \n1位全加器fa_13_si ,
       \n1位全加器fa_14_cout , \n1位全加器fa_14_si , \n1位全加器fa_15_cout , \n1位全加器fa_15_si , \n1位全加器fa_16_cout ,
       \n1位全加器fa_17_cout , \n1位全加器fa_17_si , \n1位全加器fa_18_cout , \n1位全加器fa_18_si , \n1位全加器fa_19_cout ,
       \n1位全加器fa_19_si , \n1位全加器fa_20_cout , \n1位全加器fa_20_si , \n1位全加器fa_21_cout , \n1位全加器fa_22_cout ,
       \n1位全加器fa_22_si , \n1位全加器fa_23_cout , \n1位全加器fa_23_si , \n1位全加器fa_24_cout , \n1位全加器fa_24_si ,
       \n1位全加器fa_25_cout , \n1位全加器fa_26_cout , \n1位全加器fa_26_si , \n1位全加器fa_27_cout , \n1位全加器fa_27_si ,
       \n1位全加器fa_28_cout , \n1位全加器fa_29_cout , \n1位全加器fa_29_si , \n1位全加器fa_30_cout , \n1位全加器fa_31_cout ,
       X0Y1, X0Y2, X0Y3, X0Y4, X0Y5, X1Y0, X1Y1, X1Y2, X1Y3, X1Y4, X1Y5, X2Y0, X2Y1, X2Y2, X2Y3, X2Y4, X2Y5,
       X3Y0, X3Y1, X3Y2, X3Y3, X3Y4, X3Y5, X4Y0, X4Y1, X4Y2, X4Y3, X4Y4, X4Y5, X5Y0, X5Y1, X5Y2, X5Y3, X5Y4,
       X5Y5;

  \_1位全加器FA  \u_1位全加器fa_1  (.Si(P[11]), .Cin(1'b0), .Xi(\n1位全加器fa_2_cout ), .Yi(1'b1));  // open: Cout
  \与门阵列  \u_与门阵列_1  (
    .X(X), .XY4({X5Y4, X4Y4, X3Y4, X2Y4, X1Y4, X0Y4}), .XY3({X5Y3, X4Y3, X3Y3, X2Y3, X1Y3, X0Y3}),
    .XY2({X5Y2, X4Y2, X3Y2, X2Y2, X1Y2, X0Y2}), .XY1({X5Y1, X4Y1, X3Y1, X2Y1, X1Y1, X0Y1}),
    .XY0({X5Y0, X4Y0, X3Y0, X2Y0, X1Y0, P[0]}), .Y(Y), .XY5({X5Y5, X4Y5, X3Y5, X2Y5, X1Y5, X0Y5}));
  \_1位全加器FA  \u_1位全加器fa_2  (
    .Cout(\n1位全加器fa_2_cout ), .Si(P[10]), .Cin(X5Y5), .Xi(\n1位全加器fa_4_cout ), .Yi(\n1位全加器fa_3_cout ));
  \_1位全加器FA  \u_1位全加器fa_3  (
    .Cout(\n1位全加器fa_3_cout ), .Si(\n1位全加器fa_3_si ), .Cin(X5Y4), .Xi(\n1位全加器fa_6_cout ), .Yi(\n1位全加器fa_5_cout ));
  \_1位全加器FA  \u_1位全加器fa_4  (
    .Cout(\n1位全加器fa_4_cout ), .Si(P[9]), .Cin(X4Y5), .Xi(\n1位全加器fa_7_cout ), .Yi(\n1位全加器fa_3_si ));
  \_1位全加器FA  \u_1位全加器fa_5  (
    .Cout(\n1位全加器fa_5_cout ), .Si(\n1位全加器fa_5_si ), .Cin(X5Y3), .Xi(\n1位全加器fa_9_cout ), .Yi(\n1位全加器fa_8_cout ));
  \_1位全加器FA  \u_1位全加器fa_6  (
    .Cout(\n1位全加器fa_6_cout ), .Si(\n1位全加器fa_6_si ), .Cin(X4Y4), .Xi(\n1位全加器fa_10_cout ), .Yi(\n1位全加器fa_5_si ));
  \_1位全加器FA  \u_1位全加器fa_7  (
    .Cout(\n1位全加器fa_7_cout ), .Si(P[8]), .Cin(X3Y5), .Xi(\n1位全加器fa_11_cout ), .Yi(\n1位全加器fa_6_si ));
  \_1位全加器FA  \u_1位全加器fa_8  (
    .Cout(\n1位全加器fa_8_cout ), .Si(\n1位全加器fa_8_si ), .Cin(X5Y2), .Xi(\n1位全加器fa_13_cout ),
    .Yi(\n1位全加器fa_12_cout ));
  \_1位全加器FA  \u_1位全加器fa_9  (
    .Cout(\n1位全加器fa_9_cout ), .Si(\n1位全加器fa_9_si ), .Cin(X4Y3), .Xi(\n1位全加器fa_14_cout ), .Yi(\n1位全加器fa_8_si ));
  \_1位全加器FA  \u_1位全加器fa_10  (
    .Cout(\n1位全加器fa_10_cout ), .Si(\n1位全加器fa_10_si ), .Cin(X3Y4), .Xi(\n1位全加器fa_15_cout ),
    .Yi(\n1位全加器fa_9_si ));
  \_1位全加器FA  \u_1位全加器fa_11  (
    .Cout(\n1位全加器fa_11_cout ), .Si(P[7]), .Cin(X2Y5), .Xi(\n1位全加器fa_16_cout ), .Yi(\n1位全加器fa_10_si ));
  \_1位全加器FA  \u_1位全加器fa_12  (
    .Cout(\n1位全加器fa_12_cout ), .Si(\n1位全加器fa_12_si ), .Cin(X5Y1), .Xi(\n1位全加器fa_17_cout ), .Yi(1'b1));
  \_1位全加器FA  \u_1位全加器fa_13  (
    .Cout(\n1位全加器fa_13_cout ), .Si(\n1位全加器fa_13_si ), .Cin(X4Y2), .Xi(\n1位全加器fa_18_cout ),
    .Yi(\n1位全加器fa_12_si ));
  \_1位全加器FA  \u_1位全加器fa_14  (
    .Cout(\n1位全加器fa_14_cout ), .Si(\n1位全加器fa_14_si ), .Cin(X3Y3), .Xi(\n1位全加器fa_19_cout ),
    .Yi(\n1位全加器fa_13_si ));
  \_1位全加器FA  \u_1位全加器fa_15  (
    .Cout(\n1位全加器fa_15_cout ), .Si(\n1位全加器fa_15_si ), .Cin(X2Y4), .Xi(\n1位全加器fa_20_cout ),
    .Yi(\n1位全加器fa_14_si ));
  \_1位全加器FA  \u_1位全加器fa_16  (
    .Cout(\n1位全加器fa_16_cout ), .Si(P[6]), .Cin(X1Y5), .Xi(\n1位全加器fa_21_cout ), .Yi(\n1位全加器fa_15_si ));
  \_1位全加器FA  \u_1位全加器fa_17  (
    .Cout(\n1位全加器fa_17_cout ), .Si(\n1位全加器fa_17_si ), .Cin(X4Y1), .Xi(\n1位全加器fa_22_cout ), .Yi(X5Y0));
  \_1位全加器FA  \u_1位全加器fa_18  (
    .Cout(\n1位全加器fa_18_cout ), .Si(\n1位全加器fa_18_si ), .Cin(X3Y2), .Xi(\n1位全加器fa_23_cout ),
    .Yi(\n1位全加器fa_17_si ));
  \_1位全加器FA  \u_1位全加器fa_19  (
    .Cout(\n1位全加器fa_19_cout ), .Si(\n1位全加器fa_19_si ), .Cin(X2Y3), .Xi(\n1位全加器fa_24_cout ),
    .Yi(\n1位全加器fa_18_si ));
  \_1位全加器FA  \u_1位全加器fa_20  (
    .Cout(\n1位全加器fa_20_cout ), .Si(\n1位全加器fa_20_si ), .Cin(X1Y4), .Xi(\n1位全加器fa_25_cout ),
    .Yi(\n1位全加器fa_19_si ));
  \_1位全加器FA  \u_1位全加器fa_21  (.Cout(\n1位全加器fa_21_cout ), .Si(P[5]), .Cin(X0Y5), .Xi(1'b0), .Yi(\n1位全加器fa_20_si ));
  \_1位全加器FA  \u_1位全加器fa_22  (
    .Cout(\n1位全加器fa_22_cout ), .Si(\n1位全加器fa_22_si ), .Cin(X3Y1), .Xi(\n1位全加器fa_26_cout ), .Yi(X4Y0));
  \_1位全加器FA  \u_1位全加器fa_23  (
    .Cout(\n1位全加器fa_23_cout ), .Si(\n1位全加器fa_23_si ), .Cin(X2Y2), .Xi(\n1位全加器fa_27_cout ),
    .Yi(\n1位全加器fa_22_si ));
  \_1位全加器FA  \u_1位全加器fa_24  (
    .Cout(\n1位全加器fa_24_cout ), .Si(\n1位全加器fa_24_si ), .Cin(X1Y3), .Xi(\n1位全加器fa_28_cout ),
    .Yi(\n1位全加器fa_23_si ));
  \_1位全加器FA  \u_1位全加器fa_25  (.Cout(\n1位全加器fa_25_cout ), .Si(P[4]), .Cin(X0Y4), .Xi(1'b0), .Yi(\n1位全加器fa_24_si ));
  // Probe on X
  // Probe on Y
  // Probe on P
  \_1位全加器FA  \u_1位全加器fa_26  (
    .Cout(\n1位全加器fa_26_cout ), .Si(\n1位全加器fa_26_si ), .Cin(X2Y1), .Xi(\n1位全加器fa_29_cout ), .Yi(X3Y0));
  \_1位全加器FA  \u_1位全加器fa_27  (
    .Cout(\n1位全加器fa_27_cout ), .Si(\n1位全加器fa_27_si ), .Cin(X1Y2), .Xi(\n1位全加器fa_30_cout ),
    .Yi(\n1位全加器fa_26_si ));
  \_1位全加器FA  \u_1位全加器fa_28  (.Cout(\n1位全加器fa_28_cout ), .Si(P[3]), .Cin(X0Y3), .Xi(1'b0), .Yi(\n1位全加器fa_27_si ));
  \_1位全加器FA  \u_1位全加器fa_29  (
    .Cout(\n1位全加器fa_29_cout ), .Si(\n1位全加器fa_29_si ), .Cin(X1Y1), .Xi(\n1位全加器fa_31_cout ), .Yi(X2Y0));
  \_1位全加器FA  \u_1位全加器fa_30  (.Cout(\n1位全加器fa_30_cout ), .Si(P[2]), .Cin(X0Y2), .Xi(1'b0), .Yi(\n1位全加器fa_29_si ));
  \_1位全加器FA  \u_1位全加器fa_31  (.Cout(\n1位全加器fa_31_cout ), .Si(P[1]), .Cin(X0Y1), .Xi(1'b0), .Yi(X1Y0));

  // Other names for the same wires on the sheet: X0Y0 = P[0]; XY0[5:0] = {X5Y0, X4Y0, X3Y0, X2Y0, X1Y0, P[0]};
  //   XY1[5:0] = {X5Y1, X4Y1, X3Y1, X2Y1, X1Y1, X0Y1}; XY2[5:0] = {X5Y2, X4Y2, X3Y2, X2Y2, X1Y2, X0Y2};
  //   XY3[5:0] = {X5Y3, X4Y3, X3Y3, X2Y3, X1Y3, X0Y3}; XY4[5:0] = {X5Y4, X4Y4, X3Y4, X2Y4, X1Y4, X0Y4};
  //   XY5[5:0] = {X5Y5, X4Y5, X3Y5, X2Y5, X1Y5, X0Y5}

  // Notes on the sheet:
  //   输入引脚区
  //    功能说明：6位补码阵列乘法器          输入：X（6位补码）、Y（6位补码）          输出：P（12位补码）= X×Y
  //   6位补码阵列乘法器
  //   输出引脚区
  //   验证
  //   ×
  //   =
endmodule

module \与门阵列  (
  input  [5:0] X,
  input  [5:0] Y,
  output [5:0] XY0,
  output [5:0] XY1,
  output [5:0] XY2,
  output [5:0] XY3,
  output [5:0] XY4,
  output [5:0] XY5
);

  nand nand_1 (XY0[5], X[5], Y[0]);
  nand nand_2 (XY1[5], X[5], Y[1]);
  nand nand_3 (XY2[5], X[5], Y[2]);
  nand nand_4 (XY3[5], X[5], Y[3]);
  nand nand_5 (XY4[5], X[5], Y[4]);
  and and_1 (XY5[5], X[5], Y[5]);
  and and_2 (XY0[3], X[3], Y[0]);
  and and_3 (XY0[4], X[4], Y[0]);
  and and_4 (XY1[4], X[4], Y[1]);
  and and_5 (XY1[3], X[3], Y[1]);
  and and_6 (XY2[4], X[4], Y[2]);
  and and_7 (XY2[3], X[3], Y[2]);
  and and_8 (XY3[3], X[3], Y[3]);
  and and_9 (XY3[4], X[4], Y[3]);
  and and_10 (XY4[3], X[3], Y[4]);
  and and_11 (XY4[4], X[4], Y[4]);
  nand nand_6 (XY5[4], X[4], Y[5]);
  nand nand_7 (XY5[3], X[3], Y[5]);
  and and_12 (XY0[2], X[2], Y[0]);
  and and_13 (XY1[2], X[2], Y[1]);
  and and_14 (XY2[2], X[2], Y[2]);
  and and_15 (XY3[2], X[2], Y[3]);
  and and_16 (XY4[2], X[2], Y[4]);
  nand nand_8 (XY5[2], X[2], Y[5]);
  and and_17 (XY0[1], X[1], Y[0]);
  and and_18 (XY1[1], X[1], Y[1]);
  and and_19 (XY2[1], X[1], Y[2]);
  and and_20 (XY3[1], X[1], Y[3]);
  and and_21 (XY4[1], X[1], Y[4]);
  nand nand_9 (XY5[1], X[1], Y[5]);
  and and_22 (XY0[0], X[0], Y[0]);
  and and_23 (XY1[0], X[0], Y[1]);
  and and_24 (XY2[0], X[0], Y[2]);
  and and_25 (XY3[0], X[0], Y[3]);
  and and_26 (XY4[0], X[0], Y[4]);
  nand nand_10 (XY5[0], X[0], Y[5]);

  // Other names for the same wires on the sheet: X0Y0 = XY0[0]; X1Y0 = XY0[1]; X2Y0 = XY0[2]; X3Y0 = XY0[3];
  //   X4Y0 = XY0[4]; X5Y0 = XY0[5]; X0Y1 = XY1[0]; X1Y1 = XY1[1]; X2Y1 = XY1[2]; X3Y1 = XY1[3]; X4Y1 = XY1[4];
  //   X5Y1 = XY1[5]; X0Y2 = XY2[0]; X1Y2 = XY2[1]; X2Y2 = XY2[2]; X3Y2 = XY2[3]; X4Y2 = XY2[4]; X5Y2 = XY2[5];
  //   X0Y3 = XY3[0]; X1Y3 = XY3[1]; X2Y3 = XY3[2]; X3Y3 = XY3[3]; X4Y3 = XY3[4]; X5Y3 = XY3[5]; X0Y4 = XY4[0];
  //   X1Y4 = XY4[1]; X2Y4 = XY4[2]; X3Y4 = XY4[3]; X4Y4 = XY4[4]; X5Y4 = XY4[5]; X0Y5 = XY5[0]; X1Y5 = XY5[1];
  //   X2Y5 = XY5[2]; X3Y5 = XY5[3]; X4Y5 = XY5[4]; X5Y5 = XY5[5]

  // Notes on the sheet:
  //   6位乘法与门阵列
endmodule

module \_1位全加器FA  (
  input  Cin,
  input  Xi,
  input  Yi,
  output Cout,
  output Si
);

  wire AND_2_out, AND_out, XOR_2_out;

  or OR (Cout, AND_out, AND_2_out);
  and AND (AND_out, Xi, Yi);
  and AND_2 (AND_2_out, Cin, XOR_2_out);
  xor XOR (Si, Cin, XOR_2_out);
  xor XOR_2 (XOR_2_out, Xi, Yi);

  // Notes on the sheet:
  //   Cout = Xi Yi + Cin (Xi ^ Yi)
  //   Si = Xi ^ Yi ^ Cin
  //   1位全加器（FA）
endmodule
