// Logisim project 8位原码一位乘法器.circ as structural Verilog: 6 circuits, main circuit 1位全加器（FA）
module \_8位原码一位乘法器  (
  input  [7:0] X,
  input  [7:0] Y,
  output [15:0] \乘积 
);

  wire CLK, comparator_1_eq, d_ff_1_q, END, not_1_out, RST;
  wire [0:0] \n8位串行加法器_1_s ;
  wire [3:0] counter_1_q;
  wire [7:0] multiplexer_1_out, multiplexer_2_out, \n8位串行加法器_1_cout , \X真值 , \Y真值 ;
  wire [15:0] \P真值 ;
  wire [15:15] \乘积_t ;

  Button \u_复位  (.out(RST));
  Register #(.Select("low")) register_1 (
    .D(\n8位串行加法器_1_cout ), .en(not_1_out), .Q({\乘积_t [15], \乘积 [14:8]}), .clk(CLK), .clr(RST));
  \_8位串行加法器  \u_8位串行加法器_1  (
    .X({\乘积_t [15], \乘积 [14:8]}), .Y(multiplexer_1_out), .Cin(1'b0),
    .S({\n8位串行加法器_1_cout [6:0], \n8位串行加法器_1_s [0]}), .Cout(\n8位串行加法器_1_cout [7]));  // open: out_6
  Multiplexer #(.width(8), .enable("false")) multiplexer_1 (
    .in0({8{1'b0}}), .in1({1'b0, X[6:0]}), .out(multiplexer_1_out), .sel(\乘积 [0]));
  Button u_CLK (.out(CLK));
  // Probe on {\乘积_t [15], \乘积 [14:8]}
  Multiplexer #(.width(8), .enable("false")) multiplexer_2 (
    .in0({1'b0, Y[6:0]}), .in1({\n8位串行加法器_1_s [0], \乘积 [7:1]}), .out(multiplexer_2_out), .sel(d_ff_1_q));
  // Probe on \乘积 [7:0]
  Register #(.Select("low")) Y_2 (.D(multiplexer_2_out), .en(not_1_out), .Q(\乘积 [7:0]), .clk(CLK), .clr(RST));
  Counter #(.width(4), .max('hf), .behavior("old")) counter_1 (
    .count(not_1_out), .Q(counter_1_q), .clk(CLK), .clr(RST));  // open: load, D, carry, preset
  Comparator #(.width(4), .mode("unsigned")) comparator_1 (
    .a(counter_1_q), .b(4'b1001), .eq(comparator_1_eq));  // open: gt, lt
  not not_1 (not_1_out, comparator_1_eq);
  D_Flip_Flop #(.Pre_Clr_Positions("LEGACY"), .enable("true"), .NewFFLayout("false")) d_ff_1 (
    .clk(CLK), .D(1'b1), .Q(d_ff_1_q), .reset(RST));  // open: Qn, preset, en
  LED led_1 (.in(END));
  xor xor_1 (\乘积 [15], X[7], Y[7]);
  not not_2 (END, not_1_out);
  // Probe on \P真值 
  // Probe on \X真值 
  // Probe on \Y真值 
  \_8位原码转补码  \u_8位原码转补码_1  (.X(X), .Y(\X真值 ));
  \_8位原码转补码  \u_8位原码转补码_2  (.X(Y), .Y(\Y真值 ));
  \_16位原码转补码  \u_16位原码转补码_1  (.X(\乘积 ), .Y(\P真值 ));

  // Other names for the same wires on the sheet: P[15:0] = \乘积 ; 乘积_t[14:0] = \乘积 [14:0]; X_t[6:0] = X[6:0];
  //   X原值[7:0] = X; Xs = X[7]; Y_t[6:0] = Y[6:0]; Y原值[7:0] = Y; Ys = Y[7]

  // Notes on the sheet:
  //   输入引脚区
  //   功能说明: 8位原码一位乘法器                输入：X、Y为 8位原码               输出：乘积=X*Y 为16位原码
  //   ∑
  //   首先设置X、Y值，然后按“复位”按钮，接下去按“CLK”按钮多次，直到“END”指示灯变红，此时观看乘积是不是正确？
  //   8位原码一位乘法器
  //   输出引脚区
  //   ×
  //   =
endmodule

module \_8位串行加法器  (
  input  [7:0] X,
  input  [7:0] Y,
  input  Cin,
  output [7:0] S,
  output Cout,
  output out_6
);

  wire \n1位全加器_fa_2_cout , \n1位全加器_fa_3_cout , \n1位全加器_fa_4_cout , \n1位全加器_fa_5_cout , \n1位全加器_fa_6_cout ,
       \n1位全加器_fa_7_cout , \n1位全加器_fa_8_cout ;

  xor xor_1 (out_6, Cout, \n1位全加器_fa_2_cout );
  \_1位全加器_FA  \u_1位全加器_fa_1  (.Cout(Cout), .Si(S[7]), .Cin(\n1位全加器_fa_2_cout ), .Xi(X[7]), .Yi(Y[7]));
  \_1位全加器_FA  \u_1位全加器_fa_2  (.Cout(\n1位全加器_fa_2_cout ), .Si(S[6]), .Cin(\n1位全加器_fa_3_cout ), .Xi(X[6]), .Yi(Y[6]));
  \_1位全加器_FA  \u_1位全加器_fa_3  (.Cout(\n1位全加器_fa_3_cout ), .Si(S[5]), .Cin(\n1位全加器_fa_4_cout ), .Xi(X[5]), .Yi(Y[5]));
  \_1位全加器_FA  \u_1位全加器_fa_4  (.Cout(\n1位全加器_fa_4_cout ), .Si(S[4]), .Cin(\n1位全加器_fa_5_cout ), .Xi(X[4]), .Yi(Y[4]));
  \_1位全加器_FA  \u_1位全加器_fa_5  (.Cout(\n1位全加器_fa_5_cout ), .Si(S[3]), .Cin(\n1位全加器_fa_6_cout ), .Xi(X[3]), .Yi(Y[3]));
  \_1位全加器_FA  \u_1位全加器_fa_6  (.Cout(\n1位全加器_fa_6_cout ), .Si(S[2]), .Cin(\n1位全加器_fa_7_cout ), .Xi(X[2]), .Yi(Y[2]));
  // Probe on X
  // Probe on Y
  // Probe on S
  \_1位全加器_FA  \u_1位全加器_fa_7  (.Cout(\n1位全加器_fa_7_cout ), .Si(S[1]), .Cin(\n1位全加器_fa_8_cout ), .Xi(X[1]), .Yi(Y[1]));
  // Probe on X
  // Probe on Y
  // Probe on S
  \_1位全加器_FA  \u_1位全加器_fa_8  (.Cout(\n1位全加器_fa_8_cout ), .Si(S[0]), .Cin(Cin), .Xi(X[0]), .Yi(Y[0]));

  // Other names for the same wires on the sheet: OF = out_6

  // Notes on the sheet:
  //   X: pull=down
  //   Cin: pull=down
  //   Y: pull=down
  //   输入引脚区
  //   符号位
  //   输出引脚区
  //   8位串行加法器
  //   OF
  //   +
  //   有符号加法
  //   +
  //   =
  //   无符号加法
endmodule

// FA
module \_1位全加器_FA  (
  input  Cin,
  input  Xi,
  input  Yi,
  output Cout,
  output Si
);

  wire AND_2_out, AND_out, XOR_2_out;

  and AND (AND_out, Xi, Yi);
  or OR (Cout, AND_out, AND_2_out);
  and AND_2 (AND_2_out, Cin, XOR_2_out);
  xor XOR (Si, Cin, XOR_2_out);
  xor XOR_2 (XOR_2_out, Xi, Yi);

  // Notes on the sheet:
  //   Cin: pull=down
  //   Xi: pull=down
  //   Yi: pull=down
  //   Cout = Xi Yi + Cin (Xi ^ Yi)
  //   Si = Xi ^ Yi ^ Cin
  //   1位全加器（FA）
endmodule

module \_1位全加器FA  (
  input  Cin,
  input  Xi,
  input  Yi,
  output Cout,
  output Si
);

  wire AND_2_out, AND_out, XOR_2_out;

  or OR (Cout, AND_out, AND_2_out);
  and AND (AND_out, Xi, Yi);
  and AND_2 (AND_2_out, Cin, XOR_2_out);
  xor XOR (Si, Cin, XOR_2_out);
  xor XOR_2 (XOR_2_out, Xi, Yi);

  // Notes on the sheet:
  //   Cout = Xi Yi + Cin (Xi ^ Yi)
  //   Si = Xi ^ Yi ^ Cin
  //   1位全加器（FA）
endmodule

module \_8位原码转补码  (
  input  [7:0] X,
  output [7:0] Y
);

  wire \n1位全加器fa_1_cout , \n1位全加器fa_2_cout , \n1位全加器fa_3_cout , \n1位全加器fa_4_cout , \n1位全加器fa_5_cout ,
       \n1位全加器fa_6_cout , \n1位全加器fa_7_cout , xor_2_out, xor_3_out, xor_4_out, xor_5_out, xor_6_out,
       xor_7_out, xor_8_out;

  xor xor_1 (Y[7], X[7], \n1位全加器fa_1_cout );
  xor xor_2 (xor_2_out, X[7], X[6]);
  \_1位全加器FA  \u_1位全加器fa_1  (.Cout(\n1位全加器fa_1_cout ), .Si(Y[6]), .Cin(\n1位全加器fa_2_cout ), .Xi(1'b0), .Yi(xor_2_out));
  xor xor_3 (xor_3_out, X[7], X[5]);
  xor xor_4 (xor_4_out, X[7], X[4]);
  \_1位全加器FA  \u_1位全加器fa_2  (.Cout(\n1位全加器fa_2_cout ), .Si(Y[5]), .Cin(\n1位全加器fa_3_cout ), .Xi(1'b0), .Yi(xor_3_out));
  \_1位全加器FA  \u_1位全加器fa_3  (.Cout(\n1位全加器fa_3_cout ), .Si(Y[4]), .Cin(\n1位全加器fa_4_cout ), .Xi(1'b0), .Yi(xor_4_out));
  xor xor_5 (xor_5_out, X[7], X[3]);
  \_1位全加器FA  \u_1位全加器fa_4  (.Cout(\n1位全加器fa_4_cout ), .Si(Y[3]), .Cin(\n1位全加器fa_5_cout ), .Xi(1'b0), .Yi(xor_5_out));
  xor xor_6 (xor_6_out, X[7], X[2]);
  xor xor_7 (xor_7_out, X[7], X[1]);
  \_1位全加器FA  \u_1位全加器fa_5  (.Cout(\n1位全加器fa_5_cout ), .Si(Y[2]), .Cin(\n1位全加器fa_6_cout ), .Xi(1'b0), .Yi(xor_6_out));
  \_1位全加器FA  \u_1位全加器fa_6  (.Cout(\n1位全加器fa_6_cout ), .Si(Y[1]), .Cin(\n1位全加器fa_7_cout ), .Xi(1'b0), .Yi(xor_7_out));
  xor xor_8 (xor_8_out, X[7], X[0]);
  \_1位全加器FA  \u_1位全加器fa_7  (.Cout(\n1位全加器fa_7_cout ), .Si(Y[0]), .Cin(X[7]), .Xi(1'b0), .Yi(xor_8_out));

  // Other names for the same wires on the sheet: Xj[6:0] = X[6:0]; Xs = X[7]; Yj[6:0] = Y[6:0]; Ys = Y[7]

  // Notes on the sheet:
  //   输入引脚区
  //    功能说明：8位原码转补码          输入：X（8位原码）          输出：Y（8位补码）
  //   输出引脚区
endmodule

module \_16位原码转补码  (
  input  [15:0] X,
  output [15:0] Y
);

  wire \n1位全加器fa_1_cout , \n1位全加器fa_2_cout , \n1位全加器fa_3_cout , \n1位全加器fa_4_cout , \n1位全加器fa_5_cout ,
       \n1位全加器fa_6_cout , \n1位全加器fa_7_cout , \n1位全加器fa_8_cout , \n1位全加器fa_9_cout , \n1位全加器fa_10_cout ,
       \n1位全加器fa_11_cout , \n1位全加器fa_12_cout , \n1位全加器fa_13_cout , \n1位全加器fa_14_cout , \n1位全加器fa_15_cout ,
       xor_2_out, xor_3_out, xor_4_out, xor_5_out, xor_6_out, xor_7_out, xor_8_out, xor_9_out, xor_10_out,
       xor_11_out, xor_12_out, xor_13_out, xor_14_out, xor_15_out, xor_16_out;

  xor xor_1 (Y[15], X[15], \n1位全加器fa_1_cout );
  xor xor_2 (xor_2_out, X[15], X[14]);
  \_1位全加器FA  \u_1位全加器fa_1  (.Cout(\n1位全加器fa_1_cout ), .Si(Y[14]), .Cin(\n1位全加器fa_2_cout ), .Xi(1'b0), .Yi(xor_2_out));
  xor xor_3 (xor_3_out, X[15], X[13]);
  \_1位全加器FA  \u_1位全加器fa_2  (.Cout(\n1位全加器fa_2_cout ), .Si(Y[13]), .Cin(\n1位全加器fa_4_cout ), .Xi(1'b0), .Yi(xor_3_out));
  xor xor_4 (xor_4_out, X[15], X[12]);
  xor xor_5 (xor_5_out, X[15], X[11]);
  \_1位全加器FA  \u_1位全加器fa_3  (.Cout(\n1位全加器fa_3_cout ), .Si(Y[11]), .Cin(\n1位全加器fa_6_cout ), .Xi(1'b0), .Yi(xor_5_out));
  \_1位全加器FA  \u_1位全加器fa_4  (.Cout(\n1位全加器fa_4_cout ), .Si(Y[12]), .Cin(\n1位全加器fa_3_cout ), .Xi(1'b0), .Yi(xor_4_out));
  xor xor_6 (xor_6_out, X[15], X[10]);
  xor xor_7 (xor_7_out, X[15], X[9]);
  \_1位全加器FA  \u_1位全加器fa_5  (.Cout(\n1位全加器fa_5_cout ), .Si(Y[9]), .Cin(\n1位全加器fa_7_cout ), .Xi(1'b0), .Yi(xor_7_out));
  \_1位全加器FA  \u_1位全加器fa_6  (.Cout(\n1位全加器fa_6_cout ), .Si(Y[10]), .Cin(\n1位全加器fa_5_cout ), .Xi(1'b0), .Yi(xor_6_out));
  xor xor_8 (xor_8_out, X[15], X[8]);
  \_1位全加器FA  \u_1位全加器fa_7  (.Cout(\n1位全加器fa_7_cout ), .Si(Y[8]), .Cin(\n1位全加器fa_8_cout ), .Xi(1'b0), .Yi(xor_8_out));
  xor xor_9 (xor_9_out, X[15], X[7]);
  xor xor_10 (xor_10_out, X[15], X[6]);
  \_1位全加器FA  \u_1位全加器fa_8  (.Cout(\n1位全加器fa_8_cout ), .Si(Y[7]), .Cin(\n1位全加器fa_9_cout ), .Xi(1'b0), .Yi(xor_9_out));
  \_1位全加器FA  \u_1位全加器fa_9  (.Cout(\n1位全加器fa_9_cout ), .Si(Y[6]), .Cin(\n1位全加器fa_10_cout ), .Xi(1'b0), .Yi(xor_10_out));
  xor xor_11 (xor_11_out, X[15], X[5]);
  \_1位全加器FA  \u_1位全加器fa_10  (
    .Cout(\n1位全加器fa_10_cout ), .Si(Y[5]), .Cin(\n1位全加器fa_11_cout ), .Xi(1'b0), .Yi(xor_11_out));
  xor xor_12 (xor_12_out, X[15], X[4]);
  xor xor_13 (xor_13_out, X[15], X[3]);
  \_1位全加器FA  \u_1位全加器fa_11  (
    .Cout(\n1位全加器fa_11_cout ), .Si(Y[4]), .Cin(\n1位全加器fa_12_cout ), .Xi(1'b0), .Yi(xor_12_out));
  \_1位全加器FA  \u_1位全加器fa_12  (
    .Cout(\n1位全加器fa_12_cout ), .Si(Y[3]), .Cin(\n1位全加器fa_14_cout ), .Xi(1'b0), .Yi(xor_13_out));
  xor xor_14 (xor_14_out, X[15], X[2]);
  xor xor_15 (xor_15_out, X[15], X[1]);
  \_1位全加器FA  \u_1位全加器fa_13  (
    .Cout(\n1位全加器fa_13_cout ), .Si(Y[1]), .Cin(\n1位全加器fa_15_cout ), .Xi(1'b0), .Yi(xor_15_out));
  \_1位全加器FA  \u_1位全加器fa_14  (
    .Cout(\n1位全加器fa_14_cout ), .Si(Y[2]), .Cin(\n1位全加器fa_13_cout ), .Xi(1'b0), .Yi(xor_14_out));
  xor xor_16 (xor_16_out, X[15], X[0]);
  \_1位全加器FA  \u_1位全加器fa_15  (.Cout(\n1位全加器fa_15_cout ), .Si(Y[0]), .Cin(X[15]), .Xi(1'b0), .Yi(xor_16_out));

  // Other names for the same wires on the sheet: Xj[14:0] = X[14:0]; Xs = X[15]; Yj[14:0] = Y[14:0]; Ys = Y[15]

  // Notes on the sheet:
  //   输入引脚区
  //    功能说明：16位原码转补码          输入：X（16位原码）          输出：Y（16位补码）
  //   输出引脚区
endmodule
