// Logisim project 8位补码一位乘法器（采用8位无符号一位乘法器实现）.circ as structural Verilog: 4 circuits, main circuit 1位全加器（FA）
// 8位无符号一位乘法器
module \_8位无符号数一位乘法器  (
  input  [7:0] X,
  input  [7:0] Y,
  input  \复位 ,
  input  CLK,
  output [15:0] \乘积 ,
  output END
);

  wire CLK_out, CLK_t, comparator_1_eq, d_ff_1_q, not_1_out, RST, \复位_out ;
  wire [0:0] \n8位串行加法器_1_s ;
  wire [3:0] counter_1_q;
  wire [7:0] multiplexer_1_out, multiplexer_2_out, \n8位串行加法器_1_cout ;

  Button \u_复位  (.out(\复位_out ));
  or or_1 (RST, \复位_out , \复位 );
  // Probe on \乘积 [15:8]
  Register #(.Select("low")) register_1 (.D(\n8位串行加法器_1_cout ), .en(not_1_out), .Q(\乘积 [15:8]), .clk(CLK_t), .clr(RST));
  \_8位串行加法器  \u_8位串行加法器_1  (
    .X(\乘积 [15:8]), .Y(multiplexer_1_out), .Cin(1'b0), .S({\n8位串行加法器_1_cout [6:0], \n8位串行加法器_1_s [0]}),
    .Cout(\n8位串行加法器_1_cout [7]));  // open: out_6
  Multiplexer #(.width(8), .enable("false")) multiplexer_1 (
    .in0({8{1'b0}}), .in1(X), .out(multiplexer_1_out), .sel(\乘积 [0]));
  Button u_CLK (.out(CLK_out));
  or or_2 (CLK_t, CLK_out, CLK);
  Multiplexer #(.width(8), .enable("false")) multiplexer_2 (
    .in0(Y), .in1({\n8位串行加法器_1_s [0], \乘积 [7:1]}), .out(multiplexer_2_out), .sel(d_ff_1_q));
  // Probe on \乘积 [7:0]
  Register #(.Select("low")) Y_2 (.D(multiplexer_2_out), .en(not_1_out), .Q(\乘积 [7:0]), .clk(CLK_t), .clr(RST));
  Counter #(.width(4), .max('hf), .behavior("old")) counter_1 (
    .count(not_1_out), .Q(counter_1_q), .clk(CLK_t), .clr(RST));  // open: load, D, carry, preset
  D_Flip_Flop #(.Pre_Clr_Positions("LEGACY"), .enable("true"), .NewFFLayout("false")) d_ff_1 (
    .clk(CLK_t), .D(1'b1), .Q(d_ff_1_q), .reset(RST));  // open: Qn, preset, en
  Comparator #(.width(4), .mode("unsigned")) comparator_1 (
    .a(counter_1_q), .b(4'b1001), .eq(comparator_1_eq));  // open: gt, lt
  not not_1 (not_1_out, comparator_1_eq);
  LED led_1 (.in(END));
  not not_2 (END, not_1_out);
  // Probe on X
  // Probe on Y
  // Probe on \乘积 

  // Notes on the sheet:
  //   复位: pull=down
  //   CLK: pull=down
  //   输入引脚区
  //   ∑
  //   功能说明: 8位无符号数一位乘法器                输入：X、Y 为8位无符号数               输出：乘积=X*Y 为16位无符号数
  //   首先设置X、Y值，然后按“复位”按钮，接下去按“CLK”按钮多次，直到“END”指示灯变红，此时观看乘积是不是正确？
  //   8位无符号数一位乘法器
  //   输出引脚区
  //   ×
  //   =
endmodule

module \_8位补码一位乘法器_用8位无符号数一位乘法器实现  (
  input  [7:0] X,
  input  [7:0] Y,
  output [15:0] \乘积 
);

  wire CLK, END, \n8位无符号数一位乘法器_1_end , or_2_out, RST, xor_1_out;
  wire [1:0] comparator_1_eq;
  wire [6:0] multiplexer_1_out, multiplexer_2_out;
  wire [7:0] adder_1_out, adder_2_out, not_1_out, not_2_out;
  wire [15:0] adder_3_out, adder_4_out, adder_5_out, multiplexer_3_out, \n8位无符号数一位乘法器_1_乘积 , not_3_out,
       not_4_out, not_5_out;

  // Probe on X
  assign not_1_out = ~X;  // NOT_Gate not_1, 8 bits wide
  Adder adder_1 (.a(not_1_out), .b(8'h1), .out(adder_1_out));  // open: cin, cout
  assign not_2_out = ~Y;  // NOT_Gate not_2, 8 bits wide
  Adder adder_2 (.a(not_2_out), .b(8'h1), .out(adder_2_out));  // open: cin, cout
  // Probe on Y
  Multiplexer #(.width(7), .enable("false")) multiplexer_1 (
    .in0(X[6:0]), .in1(adder_1_out[6:0]), .out(multiplexer_1_out), .sel(X[7]));
  Multiplexer #(.width(7), .enable("false")) multiplexer_2 (
    .in0(Y[6:0]), .in1(adder_2_out[6:0]), .out(multiplexer_2_out), .sel(Y[7]));
  Button \u_复位  (.out(RST));
  xor xor_1 (xor_1_out, X[7], Y[7]);
  or or_1 (END, or_2_out, \n8位无符号数一位乘法器_1_end );
  \_8位无符号数一位乘法器  \u_8位无符号数一位乘法器_1  (
    .X({1'b0, multiplexer_1_out}), .Y({1'b0, multiplexer_2_out}), .\乘积 (\n8位无符号数一位乘法器_1_乘积 ), .\复位 (RST),
    .CLK(CLK), .END(\n8位无符号数一位乘法器_1_end ));
  Button \u_时钟  (.out(CLK));
  or or_2 (or_2_out, comparator_1_eq[1], comparator_1_eq[0]);
  assign not_3_out = ~\n8位无符号数一位乘法器_1_乘积 ;  // NOT_Gate not_3, 16 bits wide
  Adder #(.width(16)) adder_3 (.a(not_3_out), .b(16'h1), .out(adder_3_out));  // open: cin, cout
  // Probe on \乘积 
  Multiplexer #(.width(16), .enable("false")) multiplexer_3 (
    .in0(\n8位无符号数一位乘法器_1_乘积 ), .in1(adder_3_out), .out(multiplexer_3_out), .sel(xor_1_out));
  assign not_4_out = ~{1'b0, Y, {7{1'b0}}};  // NOT_Gate not_4, 16 bits wide
  Adder #(.width(16)) adder_4 (.a(not_4_out), .b(16'h1), .out(adder_4_out));  // open: cin, cout
  assign not_5_out = ~{1'b0, X, {7{1'b0}}};  // NOT_Gate not_5, 16 bits wide
  Adder #(.width(16)) adder_5 (.a(not_5_out), .b(16'h1), .out(adder_5_out));  // open: cin, cout
  Comparator comparator_1 (.a(X), .b(8'h80), .eq(comparator_1_eq[0]));  // open: gt, lt
  Comparator comparator_2 (.a(Y), .b(8'h80), .eq(comparator_1_eq[1]));  // open: gt, lt
  Multiplexer #(.select(2), .width(16), .enable("false")) multiplexer_4 (
    .in0(multiplexer_3_out), .in1(adder_4_out), .in2(adder_5_out), .in3(16'h4000), .out(\乘积 ),
    .sel(comparator_1_eq));
  LED led_1 (.in(END));
  // Probe on X
  // Probe on Y
  // Probe on \乘积 

  // Notes on the sheet:
  //   输入引脚区
  //   首先设置X、Y值，然后按“复位”按钮，接下去按“CLK”按钮多次，直到“END”指示灯变红，此时观看乘积是不是正确？
  //   功能说明: 8位补码一位乘法器（用8位无符号数一位乘法器实现）                输入：X、Y 为8位补码               输出：乘积=X*Y 为16位补码
  //   8位补码一位乘法器（用8位无符号数一位乘法器实现）
  //   输出引脚区
  //   ×
  //   =
endmodule

module \_8位串行加法器  (
  input  [7:0] X,
  input  [7:0] Y,
  input  Cin,
  output [7:0] S,
  output Cout,
  output out_6
);

  wire \n1位全加器_fa_2_cout , \n1位全加器_fa_3_cout , \n1位全加器_fa_4_cout , \n1位全加器_fa_5_cout , \n1位全加器_fa_6_cout ,
       \n1位全加器_fa_7_cout , \n1位全加器_fa_8_cout ;

  xor xor_1 (out_6, Cout, \n1位全加器_fa_2_cout );
  \_1位全加器_FA  \u_1位全加器_fa_1  (.Cout(Cout), .Si(S[7]), .Cin(\n1位全加器_fa_2_cout ), .Xi(X[7]), .Yi(Y[7]));
  \_1位全加器_FA  \u_1位全加器_fa_2  (.Cout(\n1位全加器_fa_2_cout ), .Si(S[6]), .Cin(\n1位全加器_fa_3_cout ), .Xi(X[6]), .Yi(Y[6]));
  \_1位全加器_FA  \u_1位全加器_fa_3  (.Cout(\n1位全加器_fa_3_cout ), .Si(S[5]), .Cin(\n1位全加器_fa_4_cout ), .Xi(X[5]), .Yi(Y[5]));
  \_1位全加器_FA  \u_1位全加器_fa_4  (.Cout(\n1位全加器_fa_4_cout ), .Si(S[4]), .Cin(\n1位全加器_fa_5_cout ), .Xi(X[4]), .Yi(Y[4]));
  \_1位全加器_FA  \u_1位全加器_fa_5  (.Cout(\n1位全加器_fa_5_cout ), .Si(S[3]), .Cin(\n1位全加器_fa_6_cout ), .Xi(X[3]), .Yi(Y[3]));
  \_1位全加器_FA  \u_1位全加器_fa_6  (.Cout(\n1位全加器_fa_6_cout ), .Si(S[2]), .Cin(\n1位全加器_fa_7_cout ), .Xi(X[2]), .Yi(Y[2]));
  // Probe on X
  // Probe on Y
  // Probe on S
  \_1位全加器_FA  \u_1位全加器_fa_7  (.Cout(\n1位全加器_fa_7_cout ), .Si(S[1]), .Cin(\n1位全加器_fa_8_cout ), .Xi(X[1]), .Yi(Y[1]));
  // Probe on X
  // Probe on Y
  // Probe on S
  \_1位全加器_FA  \u_1位全加器_fa_8  (.Cout(\n1位全加器_fa_8_cout ), .Si(S[0]), .Cin(Cin), .Xi(X[0]), .Yi(Y[0]));

  // Other names for the same wires on the sheet: OF = out_6

  // Notes on the sheet:
  //   Y: pull=down
  //   X: pull=down
  //   Cin: pull=down
  //   输入引脚区
  //   符号位
  //   输出引脚区
  //   8位串行加法器
  //   OF
  //   +
  //   有符号加法
  //   +
  //   =
  //   无符号加法
endmodule

// FA
module \_1位全加器_FA  (
  input  Cin,
  input  Xi,
  input  Yi,
  output Cout,
  output Si
);

  wire AND_2_out, AND_out, XOR_2_out;

  and AND (AND_out, Xi, Yi);
  or OR (Cout, AND_out, AND_2_out);
  and AND_2 (AND_2_out, Cin, XOR_2_out);
  xor XOR (Si, Cin, XOR_2_out);
  xor XOR_2 (XOR_2_out, Xi, Yi);

  // Notes on the sheet:
  //   Xi: pull=down
  //   Yi: pull=down
  //   Cin: pull=down
  //   Cout = Xi Yi + Cin (Xi ^ Yi)
  //   Si = Xi ^ Yi ^ Cin
  //   1位全加器（FA）
endmodule
